// Logisim project opdracht3_nand_gates.circ as structural Verilog: 1 circuit, main circuit main
module main (
  input  input_A,
  input  input_B,
  input  input_A_2,
  input  input_B_2,
  input  input_A_3,
  input  input_A_4,
  input  input_B_3,
  output output_AB,
  output out_9,
  output out_10,
  output out_11
);

  wire and_1_out, and_2_out, and_3_out, and_4_out, and_5_out, and_6_out, and_7_out, not_2_out, not_4_out,
       not_5_out;

  and and_1 (and_1_out, input_A, input_B);
  not not_1 (output_AB, and_1_out);
  not not_2 (not_2_out, and_2_out);
  and and_2 (and_2_out, input_A_2, input_B_2);
  and and_3 (and_3_out, input_A_3, input_A_3);
  not not_3 (out_10, and_3_out);
  and and_4 (and_4_out, input_A_4, input_A_4);
  not not_4 (not_4_out, and_4_out);
  not not_5 (not_5_out, and_5_out);
  and and_5 (and_5_out, input_B_3, input_B_3);
  not not_6 (out_9, and_6_out);
  and and_6 (and_6_out, not_2_out, not_2_out);
  and and_7 (and_7_out, not_4_out, not_5_out);
  not not_7 (out_11, and_7_out);

  // Notes on the sheet:
  //   NAND
  //   AND
  //   NOT
  //   OR
endmodule
