// Logisim project ALU_Group35.circ as structural Verilog: 14 circuits, main circuit main
module main (
  output halt,
  output [8:0] counter,
  output [3:0] op,
  output [15:0] a,
  output [15:0] b,
  output [15:0] oracle,
  output [15:0] result,
  output err_oracle,
  output error,
  output ok,
  output start_delimiter
);

  wire and_1_out, and_2_out, clock_1_out, comparator_1_eq, comparator_2_eq;

  Clock clock_1 (.out(clock_1_out));
  Counter #(.width(9), .max('h1ff), .trigger("falling")) counter_1 (
    .Q(counter), .carry(halt), .clk(clock_1_out));  // open: load, D, count, clr
  RAM #(.addrWidth(12), .dataWidth(4), .bus("separate")) ram_1 (
    .addr({counter, 3'b000}), .data(op), .ld(1'b1));  // open: din, str, sel, clk, clr
  RAM #(.addrWidth(12), .dataWidth(16), .bus("separate")) ram_2 (
    .addr({counter, 3'b001}), .data(a), .ld(1'b1));  // open: din, str, sel, clk, clr
  RAM #(.addrWidth(12), .dataWidth(16), .bus("separate")) ram_3 (
    .addr({counter, 3'b010}), .data(b), .ld(1'b1));  // open: din, str, sel, clk, clr
  RAM #(.addrWidth(12), .dataWidth(16), .bus("separate")) ram_4 (
    .addr({counter, 3'b011}), .data(oracle), .ld(1'b1));  // open: din, str, sel, clk, clr
  RAM #(.addrWidth(12), .dataWidth(1), .bus("separate")) ram_5 (
    .addr({counter, 3'b100}), .data(err_oracle), .ld(1'b1));  // open: din, str, sel, clk, clr
  RAM #(.addrWidth(12), .dataWidth(1), .bus("separate")) ram_6 (
    .addr({counter, 3'b101}), .data(start_delimiter), .ld(1'b1));  // open: din, str, sel, clk, clr
  _16_bit_ALU u_16_bit_alu_1 (.ALU_code(op), .a(a), .b(b), .overflow(error), .result(result));
  Comparator #(.width(1), .mode("unsigned")) comparator_1 (
    .a(error), .b(err_oracle), .eq(comparator_1_eq));  // open: gt, lt
  Comparator #(.width(16)) comparator_2 (.a(result), .b(oracle), .eq(comparator_2_eq));  // open: gt, lt
  and and_1 (and_1_out, comparator_1_eq, error);
  and and_2 (and_2_out, comparator_2_eq, comparator_1_eq, ~error);  // AND_Gate
  or or_1 (ok, and_1_out, and_2_out);

  // Notes on the sheet:
  //   You must complete the circuit '16-bit ALU' instead.
  //   DO NOT EDIT THIS CIRCUIT!
endmodule

module _16_bit_ALU (
  input  [3:0] ALU_code,
  input  [15:0] a,
  input  [15:0] b,
  output [15:0] result,
  output overflow
);

  wire add_1_overflow, inv_1_overflow, sla_1_overflow, sub_1_overflow;
  wire [15:0] add_1_output, and_out, eq_1_out_3, gt_1_output, inv_1_output, lt_1_output, neq_1_out_3,
       not_out, or_out, sla_1_output, sll_1_output, slr_1_output, sra_1_output, sub_1_output;

  assign not_out = ~a;  // NOT_Gate not, 16 bits wide
  assign and_out = a & b;  // AND_Gate and, 16 bits wide
  assign or_out = a | b;  // OR_Gate or, 16 bits wide
  add add_1 (.A(a), .B(b), .OUTPUT(add_1_output), .OVERFLOW(add_1_overflow));
  sub sub_1 (.A(a), .B(b), .OUTPUT(sub_1_output), .OVERFLOW(sub_1_overflow));
  lt lt_1 (.A(a), .B(b), .OUTPUT(lt_1_output));
  gt gt_1 (.A(a), .B(b), .OUTPUT(gt_1_output));
  eq eq_1 (.A(a), .B(b), .out_3(eq_1_out_3));
  neq neq_1 (.A(a), .B(b), .out_3(neq_1_out_3));
  inv inv_1 (.INPUT(a), .OUTPUT(inv_1_output), .OVERFLOW(inv_1_overflow));
  sll sll_1 (.INPUT(a), .OUTPUT(sll_1_output));
  slr slr_1 (.INPUT(a), .OUTPUT(slr_1_output));
  sla sla_1 (.INPUT(a), .OUTPUT(sla_1_output), .OVERFLOW(sla_1_overflow));
  sra sra_1 (.INPUT(a), .OUTPUT(sra_1_output));
  Multiplexer #(.select(4), .width(16), .enable("false")) multiplexer_1 (
    .in0({16{1'b0}}), .in1(not_out), .in2(and_out), .in3(or_out), .in4(add_1_output), .in5(sub_1_output),
    .in6(lt_1_output), .in7(gt_1_output), .in8(eq_1_out_3), .in9(neq_1_out_3), .in10(inv_1_output),
    .in11(sll_1_output), .in12(slr_1_output), .in13(sla_1_output), .in14(sra_1_output), .in15(a),
    .out(result), .sel(ALU_code));
  Multiplexer #(.select(4), .enable("false")) multiplexer_2 (
    .in0(1'b0), .in1(1'b0), .in2(1'b0), .in3(1'b0), .in4(add_1_overflow), .in5(sub_1_overflow), .in6(1'b0),
    .in7(1'b0), .in8(1'b0), .in9(1'b0), .in10(inv_1_overflow), .in11(1'b0), .in12(1'b0),
    .in13(sla_1_overflow), .in14(1'b0), .in15(1'b0), .out(overflow), .sel(ALU_code));

  // Other names for the same wires on the sheet: MUX[3:0] = ALU_code

  // Notes on the sheet:
  //   This circuit is used as a block in the main circuit, and its layout must remain unchanged. The circuit called "main" should be the main circuit of this file.
  //   Do not change the circuit appearance.
  //   DO NOT CHANGE THE INPUTS AND OUTPUTS OF THIS CIRCUIT!
  //   Do not add/remove inputs or outputs. Do not even change their location or orientation.
endmodule

module add (
  input  [15:0] A,
  input  [15:0] B,
  output [15:0] OUTPUT,
  output OVERFLOW
);

  _16_bit_carry_lookahead_adder u_16_bit_carry_lookahead_adder_1 (
    .OUTPUT(OUTPUT), .A(A), .B(B), .C(1'b0), .OVERFLOW(OVERFLOW));
endmodule

module sub (
  input  [15:0] A,
  input  [15:0] B,
  output [15:0] OUTPUT,
  output OVERFLOW
);

  wire and_1_out, and_2_out, inv_1_overflow, n16_bit_carry_lookahead_adder_1_overflow;
  wire [15:0] inv_1_output;

  _16_bit_carry_lookahead_adder u_16_bit_carry_lookahead_adder_1 (
    .OUTPUT(OUTPUT), .A(A), .B(inv_1_output), .C(1'b0), .OVERFLOW(n16_bit_carry_lookahead_adder_1_overflow));
  inv inv_1 (.INPUT(B), .OUTPUT(inv_1_output), .OVERFLOW(inv_1_overflow));
  and and_1 (and_1_out, n16_bit_carry_lookahead_adder_1_overflow, ~inv_1_overflow);  // AND_Gate
  and and_2 (and_2_out, ~n16_bit_carry_lookahead_adder_1_overflow, inv_1_overflow);  // AND_Gate
  or or_1 (OVERFLOW, and_1_out, and_2_out);
endmodule

module lt (
  input  [15:0] A,
  input  [15:0] B,
  output [15:0] OUTPUT
);

  wire and_1_out, bitselector_1_out, bitselector_2_out, bitselector_3_out, sub_1_overflow;
  wire [15:0] bit_extender_1_out, bit_extender_2_out, sub_1_output;

  sub sub_1 (.A(A), .B(B), .OUTPUT(sub_1_output), .OVERFLOW(sub_1_overflow));
  BitSelector #(.width(16)) bitselector_1 (.in(sub_1_output), .out(bitselector_1_out), .sel(4'b1111));
  BitSelector #(.width(16)) bitselector_2 (.in(A), .out(bitselector_2_out), .sel(4'b1111));
  BitSelector #(.width(16)) bitselector_3 (.in(B), .out(bitselector_3_out), .sel(4'b1111));
  assign bit_extender_1_out = {{15{1'b0}}, bitselector_1_out};  // Bit_Extender bit_extender_1
  and and_1 (and_1_out, bitselector_2_out, ~bitselector_3_out);  // AND_Gate
  assign bit_extender_2_out = {{15{1'b0}}, and_1_out};  // Bit_Extender bit_extender_2
  Multiplexer #(.width(16), .enable("false")) multiplexer_1 (
    .in0(bit_extender_1_out), .in1(bit_extender_2_out), .out(OUTPUT), .sel(sub_1_overflow));

  // Notes on the sheet:
  //   Take last bit.
endmodule

module gt (
  input  [15:0] A,
  input  [15:0] B,
  output [15:0] OUTPUT
);

  wire and_1_out, bitselector_1_out, bitselector_2_out, bitselector_3_out, sub_1_overflow;
  wire [15:0] bit_extender_1_out, bit_extender_2_out, sub_1_output;

  sub sub_1 (.A(B), .B(A), .OUTPUT(sub_1_output), .OVERFLOW(sub_1_overflow));
  BitSelector #(.width(16)) bitselector_1 (.in(sub_1_output), .out(bitselector_1_out), .sel(4'b1111));
  BitSelector #(.width(16)) bitselector_2 (.in(A), .out(bitselector_2_out), .sel(4'b1111));
  BitSelector #(.width(16)) bitselector_3 (.in(B), .out(bitselector_3_out), .sel(4'b1111));
  assign bit_extender_1_out = {{15{1'b0}}, bitselector_1_out};  // Bit_Extender bit_extender_1
  and and_1 (and_1_out, ~bitselector_2_out, bitselector_3_out);  // AND_Gate
  assign bit_extender_2_out = {{15{1'b0}}, and_1_out};  // Bit_Extender bit_extender_2
  Multiplexer #(.width(16), .enable("false")) multiplexer_1 (
    .in0(bit_extender_1_out), .in1(bit_extender_2_out), .out(OUTPUT), .sel(sub_1_overflow));

  // Notes on the sheet:
  //   Take last bit.
endmodule

module eq (
  input  [15:0] A,
  input  [15:0] B,
  output [15:0] out_3
);

  wire not_1_out, or_1_out;
  wire [15:0] sub_1_output;

  sub sub_1 (.A(A), .B(B), .OUTPUT(sub_1_output));  // open: OVERFLOW
  or or_1 (or_1_out, sub_1_output[0], sub_1_output[1], sub_1_output[2], sub_1_output[3], sub_1_output[4], sub_1_output[5], sub_1_output[6], sub_1_output[7], sub_1_output[8], sub_1_output[9], sub_1_output[10], sub_1_output[11], sub_1_output[12], sub_1_output[13], sub_1_output[14], sub_1_output[15]);
  not not_1 (not_1_out, or_1_out);
  assign out_3 = {{15{1'b0}}, not_1_out};  // Bit_Extender bit_extender_1
endmodule

module neq (
  input  [15:0] A,
  input  [15:0] B,
  output [15:0] out_3
);

  wire or_1_out;
  wire [15:0] sub_1_output;

  sub sub_1 (.A(A), .B(B), .OUTPUT(sub_1_output));  // open: OVERFLOW
  or or_1 (or_1_out, sub_1_output[0], sub_1_output[1], sub_1_output[2], sub_1_output[3], sub_1_output[4], sub_1_output[5], sub_1_output[6], sub_1_output[7], sub_1_output[8], sub_1_output[9], sub_1_output[10], sub_1_output[11], sub_1_output[12], sub_1_output[13], sub_1_output[14], sub_1_output[15]);
  assign out_3 = {{15{1'b0}}, or_1_out};  // Bit_Extender bit_extender_1
endmodule

module inv (
  input  [15:0] INPUT,
  output [15:0] OUTPUT,
  output OVERFLOW
);

  wire [15:0] not_1_out;

  assign not_1_out = ~INPUT;  // NOT_Gate not_1, 16 bits wide
  _16_bit_carry_lookahead_adder u_16_bit_carry_lookahead_adder_1 (
    .OUTPUT(OUTPUT), .A(not_1_out), .B(16'h1), .C(1'b0), .OVERFLOW(OVERFLOW));
endmodule

module sll (
  input  [15:0] INPUT,
  output [15:0] OUTPUT
);

  LED led_1 (.in(INPUT[15]));

  assign OUTPUT = {INPUT[14:0], 1'b0};
endmodule

// srl
module slr (
  input  [15:0] INPUT,
  output [15:0] OUTPUT
);

  LED led_1 (.in(INPUT[0]));

  assign OUTPUT = {1'b0, INPUT[15:1]};
endmodule

module sla (
  input  [15:0] INPUT,
  output [15:0] OUTPUT,
  output OVERFLOW
);

  sla_overflow sla_overflow_1 (.a(INPUT[15]), .b(INPUT[14]), .x(OVERFLOW));

  assign OUTPUT = {INPUT[14:0], 1'b0};
endmodule

// overflow
module sla_overflow (
  input  a,
  input  b,
  output x
);

  wire and_1_out, and_2_out, not_1_out, not_2_out;

  not not_1 (not_1_out, b);
  not not_2 (not_2_out, a);
  and and_1 (and_1_out, a, not_1_out);
  and and_2 (and_2_out, b, not_2_out);
  or or_1 (x, and_1_out, and_2_out);
endmodule

module sra (
  input  [15:0] INPUT,
  output [15:0] OUTPUT
);

  LED led_1 (.in(INPUT[0]));

  assign OUTPUT = {{2{INPUT[15]}}, INPUT[14:1]};
endmodule
