// Logisim project CLA.circ as structural Verilog: 5 circuits, main circuit 1-bit_adder
module _1_bit_adder (
  input  A,
  input  B,
  input  carryIN,
  output sum,
  output carryOut
);

  wire and_1_out, and_2_out, and_3_out, and_4_out, and_5_out, and_6_out, and_7_out, not_1_out, not_2_out,
       not_3_out, not_4_out, not_5_out, not_6_out;

  not not_1 (not_1_out, A);
  not not_2 (not_2_out, B);
  not not_3 (not_3_out, A);
  not not_4 (not_4_out, carryIN);
  not not_5 (not_5_out, B);
  not not_6 (not_6_out, carryIN);
  and and_1 (and_1_out, B, carryIN);
  and and_2 (and_2_out, A, carryIN);
  and and_3 (and_3_out, A, B);
  and and_4 (and_4_out, not_1_out, not_2_out, carryIN);
  and and_5 (and_5_out, not_3_out, B, not_4_out);
  and and_6 (and_6_out, A, not_5_out, not_6_out);
  and and_7 (and_7_out, A, B, carryIN);
  or or_1 (carryOut, and_1_out, and_2_out, and_3_out);
  or or_2 (sum, and_4_out, and_5_out, and_6_out, and_7_out);
endmodule

module _16_bit_ripple_adder (
  input  in_1,
  input  [15:0] in_2,
  input  [15:0] in_3,
  output overflow,
  output [15:0] out_5
);

  wire n1_bit_adder_1_carryout, n1_bit_adder_2_carryout, n1_bit_adder_3_carryout, n1_bit_adder_4_carryout,
       n1_bit_adder_5_carryout, n1_bit_adder_6_carryout, n1_bit_adder_7_carryout, n1_bit_adder_8_carryout,
       n1_bit_adder_9_carryout, n1_bit_adder_10_carryout, n1_bit_adder_11_carryout, n1_bit_adder_12_carryout,
       n1_bit_adder_13_carryout, n1_bit_adder_14_carryout, n1_bit_adder_15_carryout, n1_bit_adder_16_carryout;

  // OR_Gate or_1 is placed but not wired
  _1_bit_adder u_1_bit_adder_1 (
    .A(in_2[0]), .B(in_3[0]), .carryIN(in_1), .sum(out_5[0]), .carryOut(n1_bit_adder_1_carryout));
  _1_bit_adder u_1_bit_adder_2 (
    .A(in_2[1]), .B(in_3[1]), .carryIN(n1_bit_adder_1_carryout), .sum(out_5[1]),
    .carryOut(n1_bit_adder_2_carryout));
  _1_bit_adder u_1_bit_adder_3 (
    .A(in_2[2]), .B(in_3[2]), .carryIN(n1_bit_adder_2_carryout), .sum(out_5[2]),
    .carryOut(n1_bit_adder_3_carryout));
  _1_bit_adder u_1_bit_adder_4 (
    .A(in_2[3]), .B(in_3[3]), .carryIN(n1_bit_adder_3_carryout), .sum(out_5[3]),
    .carryOut(n1_bit_adder_4_carryout));
  _1_bit_adder u_1_bit_adder_5 (
    .A(in_2[4]), .B(in_3[4]), .carryIN(n1_bit_adder_4_carryout), .sum(out_5[4]),
    .carryOut(n1_bit_adder_5_carryout));
  _1_bit_adder u_1_bit_adder_6 (
    .A(in_2[5]), .B(in_3[5]), .carryIN(n1_bit_adder_5_carryout), .sum(out_5[5]),
    .carryOut(n1_bit_adder_6_carryout));
  _1_bit_adder u_1_bit_adder_7 (
    .A(in_2[6]), .B(in_3[6]), .carryIN(n1_bit_adder_6_carryout), .sum(out_5[6]),
    .carryOut(n1_bit_adder_7_carryout));
  _1_bit_adder u_1_bit_adder_8 (
    .A(in_2[7]), .B(in_3[7]), .carryIN(n1_bit_adder_7_carryout), .sum(out_5[7]),
    .carryOut(n1_bit_adder_8_carryout));
  _1_bit_adder u_1_bit_adder_9 (
    .A(in_2[8]), .B(in_3[8]), .carryIN(n1_bit_adder_8_carryout), .sum(out_5[8]),
    .carryOut(n1_bit_adder_9_carryout));
  _1_bit_adder u_1_bit_adder_10 (
    .A(in_2[9]), .B(in_3[9]), .carryIN(n1_bit_adder_9_carryout), .sum(out_5[9]),
    .carryOut(n1_bit_adder_10_carryout));
  _1_bit_adder u_1_bit_adder_11 (
    .A(in_2[10]), .B(in_3[10]), .carryIN(n1_bit_adder_10_carryout), .sum(out_5[10]),
    .carryOut(n1_bit_adder_11_carryout));
  _1_bit_adder u_1_bit_adder_12 (
    .A(in_2[11]), .B(in_3[11]), .carryIN(n1_bit_adder_11_carryout), .sum(out_5[11]),
    .carryOut(n1_bit_adder_12_carryout));
  _1_bit_adder u_1_bit_adder_13 (
    .A(in_2[12]), .B(in_3[12]), .carryIN(n1_bit_adder_12_carryout), .sum(out_5[12]),
    .carryOut(n1_bit_adder_13_carryout));
  _1_bit_adder u_1_bit_adder_14 (
    .A(in_2[13]), .B(in_3[13]), .carryIN(n1_bit_adder_13_carryout), .sum(out_5[13]),
    .carryOut(n1_bit_adder_14_carryout));
  _1_bit_adder u_1_bit_adder_15 (
    .A(in_2[14]), .B(in_3[14]), .carryIN(n1_bit_adder_14_carryout), .sum(out_5[14]),
    .carryOut(n1_bit_adder_15_carryout));
  _1_bit_adder u_1_bit_adder_16 (
    .A(in_2[15]), .B(in_3[15]), .carryIN(n1_bit_adder_15_carryout), .sum(out_5[15]),
    .carryOut(n1_bit_adder_16_carryout));
  overflow overflow_1 (.first_bit_a(in_2[15]), .first_bit_b(in_3[15]), .first_bit_sum(out_5[15]), .overlow(overflow));

  // Other names for the same wires on the sheet: input_A[15:0] = in_2; input_B[15:0] = in_3;
  //   output___sum[15:0] = out_5
endmodule

module _16_bit_carry_lookahead_adder (
  input  C,
  input  [15:0] A,
  input  [15:0] B,
  output [15:0] OUTPUT,
  output OVERFLOW
);

  wire and_1_out, and_2_out, and_3_out, and_4_out, and_5_out, and_6_out, and_7_out, and_8_out, and_9_out,
       and_10_out, C1_out, C2_out, C3_out, n4_bit_block_cla_1_g0, n4_bit_block_cla_1_p0,
       n4_bit_block_cla_2_g0, n4_bit_block_cla_2_p0, n4_bit_block_cla_3_g0, n4_bit_block_cla_3_p0,
       n4_bit_block_cla_4_g0, n4_bit_block_cla_4_p0;

  _4_bit_block_CLA u_4_bit_block_cla_1 (
    .carryIn(C), .a0(A[0]), .b0(B[0]), .a1(A[1]), .b1(B[1]), .a2(A[2]), .b2(B[2]), .a3(A[3]), .b3(B[3]),
    .P0(n4_bit_block_cla_1_p0), .G0(n4_bit_block_cla_1_g0), .s0(OUTPUT[0]), .s1(OUTPUT[1]), .s2(OUTPUT[2]),
    .s3(OUTPUT[3]));
  _4_bit_block_CLA u_4_bit_block_cla_2 (
    .carryIn(C1_out), .a0(A[4]), .b0(B[4]), .a1(A[5]), .b1(B[5]), .a2(A[6]), .b2(B[6]), .a3(A[7]), .b3(B[7]),
    .P0(n4_bit_block_cla_2_p0), .G0(n4_bit_block_cla_2_g0), .s0(OUTPUT[4]), .s1(OUTPUT[5]), .s2(OUTPUT[6]),
    .s3(OUTPUT[7]));
  _4_bit_block_CLA u_4_bit_block_cla_3 (
    .carryIn(C2_out), .a0(A[8]), .b0(B[8]), .a1(A[9]), .b1(B[9]), .a2(A[10]), .b2(B[10]), .a3(A[11]),
    .b3(B[11]), .P0(n4_bit_block_cla_3_p0), .G0(n4_bit_block_cla_3_g0), .s0(OUTPUT[8]), .s1(OUTPUT[9]),
    .s2(OUTPUT[10]), .s3(OUTPUT[11]));
  _4_bit_block_CLA u_4_bit_block_cla_4 (
    .carryIn(C3_out), .a0(A[12]), .b0(B[12]), .a1(A[13]), .b1(B[13]), .a2(A[14]), .b2(B[14]), .a3(A[15]),
    .b3(B[15]), .P0(n4_bit_block_cla_4_p0), .G0(n4_bit_block_cla_4_g0), .s0(OUTPUT[12]), .s1(OUTPUT[13]),
    .s2(OUTPUT[14]), .s3(OUTPUT[15]));
  and and_1 (and_1_out, n4_bit_block_cla_1_p0, C);
  or C1 (C1_out, n4_bit_block_cla_1_g0, and_1_out);
  and and_2 (and_2_out, n4_bit_block_cla_2_p0, n4_bit_block_cla_1_g0);
  or C2 (C2_out, n4_bit_block_cla_2_g0, and_2_out, and_5_out);
  and and_3 (and_3_out, n4_bit_block_cla_3_p0, n4_bit_block_cla_2_g0);
  or C3 (C3_out, n4_bit_block_cla_3_g0, and_3_out, and_6_out, and_7_out);
  and and_4 (and_4_out, n4_bit_block_cla_4_p0, n4_bit_block_cla_3_g0);
  // OR_Gate C3_2 has open pins: in0=n4_bit_block_cla_4_g0, in1=and_4_out, in2=and_9_out, in3=and_8_out, in4=and_10_out, out=open
  and and_5 (and_5_out, n4_bit_block_cla_2_p0, n4_bit_block_cla_1_p0, C);
  and and_6 (and_6_out, n4_bit_block_cla_3_p0, n4_bit_block_cla_2_p0, n4_bit_block_cla_1_g0);
  and and_7 (and_7_out, n4_bit_block_cla_3_p0, n4_bit_block_cla_2_p0, n4_bit_block_cla_1_p0, C);
  and and_8 (and_8_out, n4_bit_block_cla_4_p0, n4_bit_block_cla_3_p0, n4_bit_block_cla_2_p0, n4_bit_block_cla_1_g0);
  and and_9 (and_9_out, n4_bit_block_cla_4_p0, n4_bit_block_cla_3_p0, n4_bit_block_cla_2_g0);
  and and_10 (and_10_out, n4_bit_block_cla_4_p0, n4_bit_block_cla_3_p0, n4_bit_block_cla_2_p0, n4_bit_block_cla_1_p0, C);
  overflow overflow_1 (.first_bit_a(A[15]), .first_bit_b(B[15]), .first_bit_sum(OUTPUT[15]), .overlow(OVERFLOW));

  // Other names for the same wires on the sheet: input_A[15:0] = A; input_B[15:0] = B
endmodule

module _4_bit_block_CLA (
  input  carryIn,
  input  a0,
  input  b0,
  input  a1,
  input  b1,
  input  a2,
  input  b2,
  input  a3,
  input  b3,
  output P0,
  output G0,
  output s0,
  output s1,
  output s2,
  output s3
);

  wire and_2_out, and_3_out, and_4_out, and_5_out, and_6_out, and_7_out, and_8_out, and_9_out, and_10_out,
       and_11_out, and_12_out, and_13_out, and_14_out, and_15_out, and_16_out, and_17_out, and_18_out,
       and_19_out, and_20_out, and_21_out, and_22_out, and_23_out, and_24_out, and_25_out, and_26_out,
       and_27_out, nand_1_out, nand_2_out, nand_3_out, nand_4_out, nand_5_out, nand_6_out, nand_7_out,
       nand_8_out, nand_9_out, nand_10_out, nand_11_out, nand_12_out, nand_13_out, nand_14_out, nand_15_out,
       nand_16_out, nand_17_out, nand_18_out, nand_19_out, nand_20_out, nand_21_out, nand_22_out,
       nand_23_out, nand_24_out, nand_25_out, nand_26_out, nand_27_out, nand_28_out, nand_29_out,
       nand_30_out, nand_31_out, nand_32_out, nand_33_out, nand_34_out, nand_35_out, nand_36_out,
       nand_37_out, nand_38_out, nand_39_out, nand_40_out, nand_41_out, nand_42_out, or_1_out, or_2_out,
       or_3_out, or_4_out, or_5_out, or_6_out, or_7_out, or_8_out, or_9_out, or_10_out, or_11_out, or_12_out,
       or_13_out, or_14_out, or_15_out, or_16_out, or_17_out, or_18_out, or_19_out, or_20_out, or_21_out,
       or_22_out, or_23_out, or_24_out, or_25_out, or_26_out, or_27_out, or_28_out, or_29_out, or_30_out,
       or_31_out, or_32_out, or_33_out, or_34_out, or_35_out, or_37_out, or_38_out, or_39_out, or_40_out,
       or_41_out, or_42_out, or_43_out, or_44_out, or_45_out, or_46_out;

  or or_1 (or_1_out, a0, b0);
  nand nand_1 (nand_1_out, a0, b0);
  or or_2 (or_2_out, a1, b1);
  nand nand_2 (nand_2_out, a1, b1);
  or or_3 (or_3_out, a2, b2);
  nand nand_3 (nand_3_out, a2, b2);
  or or_4 (or_4_out, a3, b3);
  nand nand_4 (nand_4_out, a3, b3);
  or or_5 (or_5_out, a3, b3);
  nand nand_5 (nand_5_out, a3, b3);
  or or_6 (or_6_out, a2, b2);
  nand nand_6 (nand_6_out, a2, b2);
  or or_7 (or_7_out, a3, b3);
  nand nand_7 (nand_7_out, a3, b3);
  or or_8 (or_8_out, a1, b1);
  nand nand_8 (nand_8_out, a1, b1);
  or or_9 (or_9_out, a2, b2);
  nand nand_9 (nand_9_out, a2, b2);
  or or_10 (or_10_out, a3, b3);
  nand nand_10 (nand_10_out, a3, b3);
  or or_11 (or_11_out, a0, b0);
  nand nand_11 (nand_11_out, a0, b0);
  or or_12 (or_12_out, a0, b0);
  nand nand_12 (nand_12_out, a0, b0);
  or or_13 (or_13_out, a0, b0);
  nand nand_13 (nand_13_out, a0, b0);
  or or_14 (or_14_out, a1, b1);
  nand nand_14 (nand_14_out, a1, b1);
  or or_15 (or_15_out, a1, b1);
  nand nand_15 (nand_15_out, a1, b1);
  or or_16 (or_16_out, a0, b0);
  nand nand_16 (nand_16_out, a0, b0);
  or or_17 (or_17_out, a1, b1);
  nand nand_17 (nand_17_out, a1, b1);
  or or_18 (or_18_out, a2, b2);
  nand nand_18 (nand_18_out, a2, b2);
  or or_19 (or_19_out, a1, b1);
  nand nand_19 (nand_19_out, a1, b1);
  or or_20 (or_20_out, a2, b2);
  nand nand_20 (nand_20_out, a2, b2);
  or or_21 (or_21_out, a2, b2);
  nand nand_21 (nand_21_out, a2, b2);
  and and_1 (P0, or_1_out, nand_1_out, or_2_out, nand_2_out, or_3_out, nand_3_out, or_4_out, nand_4_out);
  and and_2 (and_2_out, a2, b2, or_5_out, nand_5_out);
  and and_3 (and_3_out, a1, b1, or_6_out, nand_6_out, or_7_out, nand_7_out);
  and and_4 (and_4_out, a0, b0, or_8_out, nand_8_out, or_9_out, nand_9_out, or_10_out, nand_10_out);
  and and_5 (and_5_out, a3, b3);
  or or_22 (or_22_out, a0, b0);
  nand nand_22 (nand_22_out, a0, b0);
  and and_6 (and_6_out, or_11_out, nand_11_out);
  and and_7 (and_7_out, or_12_out, nand_12_out, carryIn);
  and and_8 (and_8_out, a0, b0);
  or or_23 (or_23_out, a0, b0);
  nand nand_23 (nand_23_out, a0, b0);
  or or_24 (or_24_out, a1, b1);
  nand nand_24 (nand_24_out, a1, b1);
  and and_9 (and_9_out, or_13_out, nand_13_out, carryIn, or_14_out, nand_14_out);
  and and_10 (and_10_out, a0, b0, or_15_out, nand_15_out);
  and and_11 (and_11_out, a1, b1);
  or or_25 (or_25_out, a0, b0);
  nand nand_25 (nand_25_out, a0, b0);
  or or_26 (or_26_out, a1, b1);
  nand nand_26 (nand_26_out, a1, b1);
  or or_27 (or_27_out, a1, b1);
  nand nand_27 (nand_27_out, a1, b1);
  or or_28 (or_28_out, a2, b2);
  nand nand_28 (nand_28_out, a2, b2);
  and and_12 (and_12_out, or_16_out, nand_16_out, carryIn, or_17_out, nand_17_out, or_18_out, nand_18_out);
  and and_13 (and_13_out, a0, b0, or_19_out, nand_19_out, or_20_out, nand_20_out);
  and and_14 (and_14_out, a1, b1, or_21_out, nand_21_out);
  and and_15 (and_15_out, a2, b2);
  or or_29 (or_29_out, a0, b0);
  nand nand_29 (nand_29_out, a0, b0);
  or or_30 (or_30_out, a1, b1);
  nand nand_30 (nand_30_out, a1, b1);
  or or_31 (or_31_out, a2, b2);
  nand nand_31 (nand_31_out, a2, b2);
  or or_32 (or_32_out, a1, b1);
  nand nand_32 (nand_32_out, a1, b1);
  or or_33 (or_33_out, a2, b2);
  nand nand_33 (nand_33_out, a2, b2);
  or or_34 (or_34_out, a2, b2);
  nand nand_34 (nand_34_out, a2, b2);
  or or_35 (or_35_out, a3, b3);
  nand nand_35 (nand_35_out, a3, b3);
  or or_36 (G0, and_2_out, and_3_out, and_4_out, and_5_out);
  nand nand_36 (nand_36_out, or_22_out, nand_22_out, carryIn);
  or or_37 (or_37_out, carryIn, and_6_out);
  or or_38 (or_38_out, a1, b1);
  nand nand_37 (nand_37_out, a1, b1);
  or or_39 (or_39_out, and_7_out, and_8_out);
  and and_16 (and_16_out, or_23_out, nand_23_out, carryIn);
  and and_17 (and_17_out, a0, b0);
  and and_18 (and_18_out, or_24_out, nand_24_out);
  or or_40 (or_40_out, a2, b2);
  nand nand_38 (nand_38_out, a2, b2);
  or or_41 (or_41_out, and_9_out, and_10_out, and_11_out);
  and and_19 (and_19_out, or_25_out, nand_25_out, carryIn, or_26_out, nand_26_out);
  and and_20 (and_20_out, a0, b0, or_27_out, nand_27_out);
  and and_21 (and_21_out, a1, b1);
  and and_22 (and_22_out, or_28_out, nand_28_out);
  or or_42 (or_42_out, a3, b3);
  nand nand_39 (nand_39_out, a3, b3);
  or or_43 (or_43_out, and_12_out, and_13_out, and_14_out, and_15_out);
  and and_23 (and_23_out, or_29_out, nand_29_out, carryIn, or_30_out, nand_30_out, or_31_out, nand_31_out);
  and and_24 (and_24_out, a0, b0, or_32_out, nand_32_out, or_33_out, nand_33_out);
  and and_25 (and_25_out, a1, b1, or_34_out, nand_34_out);
  and and_26 (and_26_out, a2, b2);
  and and_27 (and_27_out, or_35_out, nand_35_out);
  and and_28 (s0, nand_36_out, or_37_out);
  nand nand_40 (nand_40_out, or_38_out, nand_37_out, or_39_out);
  or or_44 (or_44_out, and_16_out, and_17_out, and_18_out);
  nand nand_41 (nand_41_out, or_40_out, nand_38_out, or_41_out);
  or or_45 (or_45_out, and_19_out, and_20_out, and_21_out, and_22_out);
  nand nand_42 (nand_42_out, or_42_out, nand_39_out, or_43_out);
  or or_46 (or_46_out, and_23_out, and_24_out, and_25_out, and_26_out, and_27_out);
  and and_29 (s1, nand_40_out, or_44_out);
  and and_30 (s2, nand_41_out, or_45_out);
  and and_31 (s3, nand_42_out, or_46_out);
endmodule

module overflow (
  input  first_bit_a,
  input  first_bit_b,
  input  first_bit_sum,
  output overlow
);

  wire and_1_out, and_2_out;

  and and_1 (and_1_out, ~first_bit_a, ~first_bit_b, first_bit_sum);  // AND_Gate
  and and_2 (and_2_out, ~first_bit_sum, first_bit_b, first_bit_a);  // AND_Gate
  or or_1 (overlow, and_1_out, and_2_out);
endmodule
