// Logisim project SD_Group35.circ as structural Verilog
module main (
  output [15:0] pc,
  output [15:0] r0,
  output [15:0] r1,
  output [15:0] r2,
  output [15:0] r3,
  output [15:0] r4,
  output [15:0] r5,
  output [15:0] r6,
  output [15:0] r7,
  output [15:0] r8,
  output [15:0] r9,
  output [15:0] r10,
  output [15:0] r11,
  output [15:0] r12,
  output [15:0] r13,
  output [15:0] r14,
  output [15:0] r15,
  output halt
);

  wire and_1_out, and_2_out, bit_extender_2_out, clock_1_out, control_unit_1_aluimm, control_unit_1_alusrc,
       control_unit_1_brnz, control_unit_1_j, control_unit_1_jal, control_unit_1_jr, control_unit_1_lui,
       control_unit_1_memread, control_unit_1_memwrite, control_unit_1_ori, control_unit_1_rdtort,
       control_unit_1_regdst, control_unit_1_regwrite, control_unit_1_unknown_instruction,
       control_unit_1_zero, n16_bit_alu_1_overflow, or_1_out, or_2_out, reset_out;
  wire [1:0] control_unit_1_memtoreg;
  wire [3:0] control_unit_1_alu_op_code, control_unit_1_rd, control_unit_1_rs, control_unit_1_rt,
       multiplexer_2_out, multiplexer_3_out, multiplexer_4_out;
  wire [15:0] bit_extender_1_out, immediate_unit_1_immediate_value, multiplexer_1_out, multiplexer_5_out,
       multiplexer_6_out, multiplexer_7_out, n16_bit_alu_1_result, program_counter_1_pc_1, ram_1_data,
       ram_2_data, register_file_1_s, register_file_1_t;

  Halt halt_1 (.instruction(ram_1_data), .clock(clock_1_out), .reset(reset_out), .HALT(or_1_out), .halt_2(halt));
  Clock clock_1 (.out(clock_1_out));
  or or_1 (or_1_out, n16_bit_alu_1_overflow, control_unit_1_unknown_instruction);
  Button reset (.out(reset_out));
  Multiplexer #(.width(16), .enable("false")) multiplexer_1 (
    .in0(immediate_unit_1_immediate_value), .in1(multiplexer_7_out), .out(multiplexer_1_out),
    .sel(control_unit_1_jr));
  or or_2 (or_2_out, control_unit_1_jal, control_unit_1_jr, control_unit_1_j);
  program_counter program_counter_1 (
    .C(and_1_out), .BRANCH_VALUE(multiplexer_1_out), .INSTRUCTION_ADRRESS(pc), .RESET(reset_out),
    .BRANCH_RELATIVE(and_2_out), .BRANCH_ABSOLUTE(or_2_out), .PC_1(program_counter_1_pc_1));
  and and_1 (and_1_out, ~halt, clock_1_out);  // AND_Gate
  resources_control_unit control_unit_1 (
    .INSTRUCTION(ram_1_data), .rd(control_unit_1_rd), .rs(control_unit_1_rs), .ORI(control_unit_1_ori),
    .LUI(control_unit_1_lui), .BRNZ(control_unit_1_brnz), .J(control_unit_1_j), .JR(control_unit_1_jr),
    .JAL(control_unit_1_jal), .rt(control_unit_1_rt), .MemToReg(control_unit_1_memtoreg),
    .MemRead(control_unit_1_memread), .MemWrite(control_unit_1_memwrite), .ALUSrc(control_unit_1_alusrc),
    .RegWrite(control_unit_1_regwrite), .ALUImm(control_unit_1_aluimm),
    .ALU_OP_CODE(control_unit_1_alu_op_code), .ZERO(control_unit_1_zero), .RegDst(control_unit_1_regdst),
    .rdTOrt(control_unit_1_rdtort), .UNKNOWN_INSTRUCTION(control_unit_1_unknown_instruction));
  RAM #(.addrWidth(16), .dataWidth(16)) ram_1 (
    .addr(pc), .data(ram_1_data), .clk(and_1_out), .ld(1'b1), .clr(reset_out));  // open: sel
  Multiplexer #(.width(4), .enable("false")) multiplexer_2 (
    .in0(control_unit_1_rs), .in1(4'b0000), .out(multiplexer_2_out), .sel(control_unit_1_zero));
  Multiplexer #(.width(4), .enable("false")) multiplexer_3 (
    .in0(control_unit_1_rt), .in1(control_unit_1_rd), .out(multiplexer_3_out), .sel(control_unit_1_regdst));
  Multiplexer #(.width(4), .enable("false")) multiplexer_4 (
    .in0(control_unit_1_rd), .in1(control_unit_1_rt), .out(multiplexer_4_out), .sel(control_unit_1_rdtort));
  assign bit_extender_1_out = {{12{1'b0}}, control_unit_1_rt};  // Bit_Extender bit_extender_1
  register_file register_file_1 (
    .DATA(multiplexer_7_out), .rd(multiplexer_4_out), .rt(multiplexer_3_out), .rs(multiplexer_2_out),
    .r0(r0), .r1(r1), .r2(r2), .r3(r3), .r4(r4), .r5(r5), .r6(r6), .r7(r7), .r8(r8), .r9(r9), .r10(r10),
    .r11(r11), .r12(r12), .r13(r13), .r14(r14), .r15(r15), .T(register_file_1_t), .S(register_file_1_s),
    .WRITE(control_unit_1_regwrite), .C(and_1_out), .RESET(reset_out));
  immediate_unit immediate_unit_1 (
    .INSTRUCTION(ram_1_data), .IMMEDIATE_VALUE(immediate_unit_1_immediate_value), .ORI(control_unit_1_ori),
    .LUI(control_unit_1_lui), .BRNZ(control_unit_1_brnz), .J(control_unit_1_j), .JR(control_unit_1_jr),
    .JAL(control_unit_1_jal));  // open: out_9
  Multiplexer #(.width(16), .enable("false")) multiplexer_5 (
    .in0(register_file_1_s), .in1(immediate_unit_1_immediate_value), .out(multiplexer_5_out),
    .sel(control_unit_1_aluimm));
  Multiplexer #(.width(16), .enable("false")) multiplexer_6 (
    .in0(register_file_1_t), .in1(bit_extender_1_out), .out(multiplexer_6_out), .sel(control_unit_1_alusrc));
  _16_bit_ALU u_16_bit_alu_1 (
    .ALU_code(control_unit_1_alu_op_code), .a(multiplexer_5_out), .b(multiplexer_6_out),
    .overflow(n16_bit_alu_1_overflow), .result(n16_bit_alu_1_result));
  and and_2 (and_2_out, control_unit_1_brnz, bit_extender_2_out);
  Bit_Extender #(.in_width(16), .out_width(1)) bit_extender_2 (.in(n16_bit_alu_1_result), .out(bit_extender_2_out));
  RAM #(.addrWidth(16), .dataWidth(16), .bus("separate")) ram_2 (
    .addr(n16_bit_alu_1_result), .din(register_file_1_t), .data(ram_2_data), .str(control_unit_1_memwrite),
    .clk(and_1_out), .ld(control_unit_1_memread), .clr(reset_out));  // open: sel
  Multiplexer #(.select(2), .width(16), .enable("false")) multiplexer_7 (
    .in0(n16_bit_alu_1_result), .in1(ram_2_data), .in2(immediate_unit_1_immediate_value),
    .in3(program_counter_1_pc_1), .out(multiplexer_7_out), .sel(control_unit_1_memtoreg));

  // Notes on the sheet:
  //   current instruction
  //   reset button
  //   clock signal
  //   overflow
  //   unknown instruction
  //   instruction memory
  //   rs
  //   rt
  //   rd
  //   write data
  //   DATA
  //   DO NOT CHANGE THE INPUTS AND OUTPUTS OF THIS CIRCUIT! Do not add/remove inputs or outputs. Do not even change their location or orientation.
  //   S
  //   T
  //   clock signal
  //   reset
  //   ALU op code
  //   immediate / signed
  //   data memory
  //   program counter + 1
  //   MemToReg
  //   write data
endmodule

module Halt (
  input  [15:0] instruction,
  input  HALT,
  input  clock,
  input  reset,
  output halt_2
);

  wire and_1_out, comparator_1_eq, comparator_2_gt, counter_1_carry, or_1_out, or_2_out, register_1_q;
  wire [11:0] counter_1_q;

  Comparator #(.width(16), .mode("unsigned")) comparator_1 (
    .a(instruction), .b({16{1'b0}}), .eq(comparator_1_eq));  // open: gt, lt
  Counter #(.width(12), .max('hfff), .trigger("falling")) counter_1 (
    .Q(counter_1_q), .carry(counter_1_carry), .clk(clock), .clr(reset));  // open: load, D, count
  or or_1 (or_1_out, comparator_1_eq, counter_1_carry);
  Comparator #(.width(12), .mode("unsigned")) comparator_2 (
    .a(counter_1_q), .b({12{1'b0}}), .gt(comparator_2_gt));  // open: eq, lt
  or or_2 (or_2_out, register_1_q, and_1_out);
  and and_1 (and_1_out, or_1_out, comparator_2_gt);
  Register #(.width(1)) register_1 (.D(or_2_out), .Q(register_1_q), .clk(clock), .clr(reset));  // open: en
  or or_3 (halt_2, register_1_q, HALT);

  // Notes on the sheet:
  //   halt becomes and stays asserted if the instruction is 0000 (not in the first clock cycle) or the end of the counter is reached (2^12)
endmodule

module program_counter (
  input  BRANCH_ABSOLUTE,
  input  C,
  input  [15:0] BRANCH_VALUE,
  input  BRANCH_RELATIVE,
  input  RESET,
  output [15:0] PC_1,
  output [15:0] INSTRUCTION_ADRRESS
);

  wire [15:0] add_2_output, multiplexer_1_out, multiplexer_2_out;

  project1_16_bit_register u_16_bit_register_1 (
    .C(C), .INPUT(multiplexer_2_out), .Q(INSTRUCTION_ADRRESS), .RESET(RESET), .WRITE(1'b1));
  add add_1 (.A(16'h1), .B(INSTRUCTION_ADRRESS), .OUTPUT(PC_1));  // open: OVERFLOW
  add add_2 (.A(PC_1), .B(BRANCH_VALUE), .OUTPUT(add_2_output));  // open: OVERFLOW
  Multiplexer #(.width(16), .enable("false")) multiplexer_1 (
    .in0(PC_1), .in1(add_2_output), .out(multiplexer_1_out), .sel(BRANCH_RELATIVE));
  Multiplexer #(.width(16), .enable("false")) multiplexer_2 (
    .in0(multiplexer_1_out), .in1(BRANCH_VALUE), .out(multiplexer_2_out), .sel(BRANCH_ABSOLUTE));

  // Notes on the sheet:
  //   WRITE ENABLE
  //   new pc value or branch address
  //   PC + 1 / (+4)
  //   target address is calculated on the current PC if 1
  //   absolute branch will jump to specified address regardless the current PC if 1
endmodule

module _16_bit_register (
  input  C,
  input  [15:0] INPUT,
  input  RESET,
  input  WRITE,
  output [15:0] Q
);

  D_Flip_Flop #(.trigger("falling")) d_ff_1 (
    .clk(C), .D(INPUT[0]), .Q(Q[0]), .en(WRITE), .reset(RESET));  // open: Qn, preset
  D_Flip_Flop #(.trigger("falling")) d_ff_2 (
    .clk(C), .D(INPUT[1]), .Q(Q[1]), .en(WRITE), .reset(RESET));  // open: Qn, preset
  D_Flip_Flop #(.trigger("falling")) d_ff_3 (
    .clk(C), .D(INPUT[2]), .Q(Q[2]), .en(WRITE), .reset(RESET));  // open: Qn, preset
  D_Flip_Flop #(.trigger("falling")) d_ff_4 (
    .clk(C), .D(INPUT[3]), .Q(Q[3]), .en(WRITE), .reset(RESET));  // open: Qn, preset
  D_Flip_Flop #(.trigger("falling")) d_ff_5 (
    .clk(C), .D(INPUT[4]), .Q(Q[4]), .en(WRITE), .reset(RESET));  // open: Qn, preset
  D_Flip_Flop #(.trigger("falling")) d_ff_6 (
    .clk(C), .D(INPUT[5]), .Q(Q[5]), .en(WRITE), .reset(RESET));  // open: Qn, preset
  D_Flip_Flop #(.trigger("falling")) d_ff_7 (
    .clk(C), .D(INPUT[6]), .Q(Q[6]), .en(WRITE), .reset(RESET));  // open: Qn, preset
  D_Flip_Flop #(.trigger("falling")) d_ff_8 (
    .clk(C), .D(INPUT[7]), .Q(Q[7]), .en(WRITE), .reset(RESET));  // open: Qn, preset
  D_Flip_Flop #(.trigger("falling")) d_ff_9 (
    .clk(C), .D(INPUT[8]), .Q(Q[8]), .en(WRITE), .reset(RESET));  // open: Qn, preset
  D_Flip_Flop #(.trigger("falling")) d_ff_10 (
    .clk(C), .D(INPUT[9]), .Q(Q[9]), .en(WRITE), .reset(RESET));  // open: Qn, preset
  D_Flip_Flop #(.trigger("falling")) d_ff_11 (
    .clk(C), .D(INPUT[10]), .Q(Q[10]), .en(WRITE), .reset(RESET));  // open: Qn, preset
  D_Flip_Flop #(.trigger("falling")) d_ff_12 (
    .clk(C), .D(INPUT[11]), .Q(Q[11]), .en(WRITE), .reset(RESET));  // open: Qn, preset
  D_Flip_Flop #(.trigger("falling")) d_ff_13 (
    .clk(C), .D(INPUT[12]), .Q(Q[12]), .en(WRITE), .reset(RESET));  // open: Qn, preset
  D_Flip_Flop #(.trigger("falling")) d_ff_14 (
    .clk(C), .D(INPUT[13]), .Q(Q[13]), .en(WRITE), .reset(RESET));  // open: Qn, preset
  D_Flip_Flop #(.trigger("falling")) d_ff_15 (
    .clk(C), .D(INPUT[14]), .Q(Q[14]), .en(WRITE), .reset(RESET));  // open: Qn, preset
  D_Flip_Flop #(.trigger("falling")) d_ff_16 (
    .clk(C), .D(INPUT[15]), .Q(Q[15]), .en(WRITE), .reset(RESET));  // open: Qn, preset
endmodule

module register_file (
  input  [15:0] DATA,
  input  [3:0] rd,
  input  WRITE,
  input  C,
  input  RESET,
  input  [3:0] rt,
  input  [3:0] rs,
  output [15:0] r0,
  output [15:0] r1,
  output [15:0] r2,
  output [15:0] r3,
  output [15:0] r4,
  output [15:0] r5,
  output [15:0] r6,
  output [15:0] r7,
  output [15:0] r8,
  output [15:0] r9,
  output [15:0] r10,
  output [15:0] r11,
  output [15:0] r12,
  output [15:0] r13,
  output [15:0] r14,
  output [15:0] r15,
  output [15:0] T,
  output [15:0] S
);

  wire and_1_out, and_2_out, and_3_out, and_4_out, and_5_out, and_6_out, and_7_out, and_8_out, and_9_out,
       and_10_out, and_11_out, and_12_out, and_13_out, and_14_out, and_15_out, and_16_out, decoder_1_out0,
       decoder_1_out1, decoder_1_out2, decoder_1_out3, decoder_1_out4, decoder_1_out5, decoder_1_out6,
       decoder_1_out7, decoder_1_out8, decoder_1_out9, decoder_1_out10, decoder_1_out11, decoder_1_out12,
       decoder_1_out13, decoder_1_out14, decoder_1_out15;

  Decoder #(.select(4), .enable("false")) decoder_1 (
    .out0(decoder_1_out0), .out1(decoder_1_out1), .out2(decoder_1_out2), .out3(decoder_1_out3),
    .out4(decoder_1_out4), .out5(decoder_1_out5), .out6(decoder_1_out6), .out7(decoder_1_out7),
    .out8(decoder_1_out8), .out9(decoder_1_out9), .out10(decoder_1_out10), .out11(decoder_1_out11),
    .out12(decoder_1_out12), .out13(decoder_1_out13), .out14(decoder_1_out14), .out15(decoder_1_out15),
    .sel(rd));
  and and_1 (and_1_out, WRITE, decoder_1_out0);
  and and_2 (and_2_out, WRITE, decoder_1_out1);
  and and_3 (and_3_out, WRITE, decoder_1_out2);
  and and_4 (and_4_out, WRITE, decoder_1_out3);
  and and_5 (and_5_out, WRITE, decoder_1_out4);
  and and_6 (and_6_out, WRITE, decoder_1_out5);
  and and_7 (and_7_out, WRITE, decoder_1_out6);
  and and_8 (and_8_out, WRITE, decoder_1_out7);
  and and_9 (and_9_out, WRITE, decoder_1_out8);
  and and_10 (and_10_out, WRITE, decoder_1_out9);
  and and_11 (and_11_out, WRITE, decoder_1_out10);
  and and_12 (and_12_out, WRITE, decoder_1_out11);
  and and_13 (and_13_out, WRITE, decoder_1_out12);
  and and_14 (and_14_out, WRITE, decoder_1_out13);
  and and_15 (and_15_out, WRITE, decoder_1_out14);
  and and_16 (and_16_out, WRITE, decoder_1_out15);
  _16_bit_register u_16_bit_register_1 (.C(C), .INPUT({16{1'b0}}), .Q(r0), .RESET(RESET), .WRITE(and_1_out));
  _16_bit_register u_16_bit_register_2 (.C(C), .INPUT(DATA), .Q(r1), .RESET(RESET), .WRITE(and_2_out));
  _16_bit_register u_16_bit_register_3 (.C(C), .INPUT(DATA), .Q(r2), .RESET(RESET), .WRITE(and_3_out));
  _16_bit_register u_16_bit_register_4 (.C(C), .INPUT(DATA), .Q(r3), .RESET(RESET), .WRITE(and_4_out));
  _16_bit_register u_16_bit_register_5 (.C(C), .INPUT(DATA), .Q(r4), .RESET(RESET), .WRITE(and_5_out));
  _16_bit_register u_16_bit_register_6 (.C(C), .INPUT(DATA), .Q(r5), .RESET(RESET), .WRITE(and_6_out));
  _16_bit_register u_16_bit_register_7 (.C(C), .INPUT(DATA), .Q(r6), .RESET(RESET), .WRITE(and_7_out));
  _16_bit_register u_16_bit_register_8 (.C(C), .INPUT(DATA), .Q(r7), .RESET(RESET), .WRITE(and_8_out));
  _16_bit_register u_16_bit_register_9 (.C(C), .INPUT(DATA), .Q(r8), .RESET(RESET), .WRITE(and_9_out));
  _16_bit_register u_16_bit_register_10 (.C(C), .INPUT(DATA), .Q(r9), .RESET(RESET), .WRITE(and_10_out));
  _16_bit_register u_16_bit_register_11 (.C(C), .INPUT(DATA), .Q(r10), .RESET(RESET), .WRITE(and_11_out));
  _16_bit_register u_16_bit_register_12 (.C(C), .INPUT(DATA), .Q(r11), .RESET(RESET), .WRITE(and_12_out));
  _16_bit_register u_16_bit_register_13 (.C(C), .INPUT(DATA), .Q(r12), .RESET(RESET), .WRITE(and_13_out));
  _16_bit_register u_16_bit_register_14 (.C(C), .INPUT(DATA), .Q(r13), .RESET(RESET), .WRITE(and_14_out));
  _16_bit_register u_16_bit_register_15 (.C(C), .INPUT(DATA), .Q(r14), .RESET(RESET), .WRITE(and_15_out));
  _16_bit_register u_16_bit_register_16 (.C(C), .INPUT(DATA), .Q(r15), .RESET(RESET), .WRITE(and_16_out));
  Multiplexer #(.select(4), .width(16), .enable("false")) multiplexer_1 (
    .in0(r0), .in1(r1), .in2(r2), .in3(r3), .in4(r4), .in5(r5), .in6(r6), .in7(r7), .in8(r8), .in9(r9),
    .in10(r10), .in11(r11), .in12(r12), .in13(r13), .in14(r14), .in15(r15), .out(T), .sel(rt));
  Multiplexer #(.select(4), .width(16), .enable("false")) multiplexer_2 (
    .in0(r0), .in1(r1), .in2(r2), .in3(r3), .in4(r4), .in5(r5), .in6(r6), .in7(r7), .in8(r8), .in9(r9),
    .in10(r10), .in11(r11), .in12(r12), .in13(r13), .in14(r14), .in15(r15), .out(S), .sel(rs));

  // Notes on the sheet:
  //   r1 ALWAYS ZERO
  //   register rt content
  //   register rs content
endmodule

module control_unit (
  input  [3:0] rt,
  input  [3:0] OP_CODE,
  output [3:0] rt_2,
  output MemToReg,
  output MemRead,
  output MemWrite,
  output ALUSrc,
  output RegWrite,
  output RegDst,
  output [3:0] ALU_CODE
);

  wire ADD_out, AND_out, CP_out, EQ_out, GT_out, INV_out, LT_out, NEQ_out, NOT_2_out, OR_out, R_TYPE_out,
       SLA_out, SLL_out, SRA_out, SRL_out, SUB_out, ZERO_out;

  and ZERO (ZERO_out, ~OP_CODE[0], ~OP_CODE[1], ~OP_CODE[2], ~OP_CODE[3]);  // AND_Gate
  and R_TYPE (R_TYPE_out, OP_CODE[0], ~OP_CODE[1], ~OP_CODE[2], ~OP_CODE[3]);  // AND_Gate
  and AND (AND_out, ~OP_CODE[0], OP_CODE[1], ~OP_CODE[2], ~OP_CODE[3]);  // AND_Gate
  and OR (OR_out, OP_CODE[0], OP_CODE[1], ~OP_CODE[2], ~OP_CODE[3]);  // AND_Gate
  or or_2 (ALU_CODE[0], OR_out, SUB_out, GT_out, NEQ_out, NOT_2_out, SLL_out, SLA_out, CP_out);
  and ADD (ADD_out, ~OP_CODE[0], ~OP_CODE[1], OP_CODE[2], ~OP_CODE[3]);  // AND_Gate
  and SUB (SUB_out, OP_CODE[0], ~OP_CODE[1], OP_CODE[2], ~OP_CODE[3]);  // AND_Gate
  and LT (LT_out, ~OP_CODE[0], OP_CODE[1], OP_CODE[2], ~OP_CODE[3]);  // AND_Gate
  and GT (GT_out, OP_CODE[0], OP_CODE[1], OP_CODE[2], ~OP_CODE[3]);  // AND_Gate
  and EQ (EQ_out, ~OP_CODE[0], ~OP_CODE[1], ~OP_CODE[2], OP_CODE[3]);  // AND_Gate
  or or_3 (ALU_CODE[1], OR_out, LT_out, GT_out, AND_out, CP_out, INV_out, SLL_out, SRA_out);
  and NEQ (NEQ_out, OP_CODE[0], ~OP_CODE[1], ~OP_CODE[2], OP_CODE[3]);  // AND_Gate
  and LW (MemRead, ~OP_CODE[0], OP_CODE[1], ~OP_CODE[2], OP_CODE[3]);  // AND_Gate
  LED led_1 (.in(OP_CODE[0]));
  LED led_2 (.in(OP_CODE[1]));
  LED led_3 (.in(OP_CODE[2]));
  LED led_4 (.in(OP_CODE[3]));
  and SW (MemWrite, OP_CODE[0], OP_CODE[1], ~OP_CODE[2], OP_CODE[3]);  // AND_Gate
  not not_1 (RegWrite, MemWrite);
  or or_4 (ALU_CODE[2], ADD_out, SUB_out, LT_out, GT_out, MemWrite, MemRead, SRL_out, SLA_out, SRA_out, CP_out);
  // AND_Gate ZERO_2 has open pins: in0=rt[0], in1=rt[1], in2=rt[2], in3=rt[3], in4=ZERO_out, out=open
  and NOT_2 (NOT_2_out, rt[0], ~rt[1], ~rt[2], ~rt[3], R_TYPE_out);  // AND_Gate
  and INV (INV_out, ~rt[0], rt[1], ~rt[2], rt[3], R_TYPE_out);  // AND_Gate
  or or_5 (ALUSrc, MemWrite, MemRead);
  and SLL (SLL_out, rt[0], rt[1], ~rt[2], rt[3], R_TYPE_out);  // AND_Gate
  and SRL (SRL_out, ~rt[0], ~rt[1], rt[2], rt[3], R_TYPE_out);  // AND_Gate
  or or_6 (ALU_CODE[3], EQ_out, NEQ_out, CP_out, INV_out, SLL_out, SRL_out, SLA_out, SRA_out);
  and SLA (SLA_out, rt[0], ~rt[1], rt[3], rt[3], R_TYPE_out);  // AND_Gate
  and SRA (SRA_out, ~rt[0], rt[1], rt[2], rt[3], R_TYPE_out);  // AND_Gate
  LED led_5 (.in(R_TYPE_out));
  LED led_6 (.in(rt[0]));
  LED led_7 (.in(rt[1]));
  LED led_8 (.in(rt[2]));
  LED led_9 (.in(rt[3]));
  and CP (CP_out, rt[0], rt[1], rt[2], rt[3], R_TYPE_out);

  assign MemToReg = MemRead;
  assign RegDst = MemWrite;
  assign rt_2 = rt;

  // Notes on the sheet:
  //   bits  12 - 15
  //   zero
  //   bits 0 - 3
  //   register operations, function depends on 0 - 3 bits
endmodule
