// Logisim project project1.circ as structural Verilog: 7 circuits, main circuit 16-bit_register
module _16_bit_register (
  input  C,
  input  [15:0] INPUT,
  input  RESET,
  input  WRITE,
  output [15:0] Q
);

  D_Flip_Flop #(.trigger("falling")) d_ff_1 (
    .clk(C), .D(INPUT[0]), .Q(Q[0]), .en(WRITE), .reset(RESET));  // open: Qn, preset
  D_Flip_Flop #(.trigger("falling")) d_ff_2 (
    .clk(C), .D(INPUT[1]), .Q(Q[1]), .en(WRITE), .reset(RESET));  // open: Qn, preset
  D_Flip_Flop #(.trigger("falling")) d_ff_3 (
    .clk(C), .D(INPUT[2]), .Q(Q[2]), .en(WRITE), .reset(RESET));  // open: Qn, preset
  D_Flip_Flop #(.trigger("falling")) d_ff_4 (
    .clk(C), .D(INPUT[3]), .Q(Q[3]), .en(WRITE), .reset(RESET));  // open: Qn, preset
  D_Flip_Flop #(.trigger("falling")) d_ff_5 (
    .clk(C), .D(INPUT[4]), .Q(Q[4]), .en(WRITE), .reset(RESET));  // open: Qn, preset
  D_Flip_Flop #(.trigger("falling")) d_ff_6 (
    .clk(C), .D(INPUT[5]), .Q(Q[5]), .en(WRITE), .reset(RESET));  // open: Qn, preset
  D_Flip_Flop #(.trigger("falling")) d_ff_7 (
    .clk(C), .D(INPUT[6]), .Q(Q[6]), .en(WRITE), .reset(RESET));  // open: Qn, preset
  D_Flip_Flop #(.trigger("falling")) d_ff_8 (
    .clk(C), .D(INPUT[7]), .Q(Q[7]), .en(WRITE), .reset(RESET));  // open: Qn, preset
  D_Flip_Flop #(.trigger("falling")) d_ff_9 (
    .clk(C), .D(INPUT[8]), .Q(Q[8]), .en(WRITE), .reset(RESET));  // open: Qn, preset
  D_Flip_Flop #(.trigger("falling")) d_ff_10 (
    .clk(C), .D(INPUT[9]), .Q(Q[9]), .en(WRITE), .reset(RESET));  // open: Qn, preset
  D_Flip_Flop #(.trigger("falling")) d_ff_11 (
    .clk(C), .D(INPUT[10]), .Q(Q[10]), .en(WRITE), .reset(RESET));  // open: Qn, preset
  D_Flip_Flop #(.trigger("falling")) d_ff_12 (
    .clk(C), .D(INPUT[11]), .Q(Q[11]), .en(WRITE), .reset(RESET));  // open: Qn, preset
  D_Flip_Flop #(.trigger("falling")) d_ff_13 (
    .clk(C), .D(INPUT[12]), .Q(Q[12]), .en(WRITE), .reset(RESET));  // open: Qn, preset
  D_Flip_Flop #(.trigger("falling")) d_ff_14 (
    .clk(C), .D(INPUT[13]), .Q(Q[13]), .en(WRITE), .reset(RESET));  // open: Qn, preset
  D_Flip_Flop #(.trigger("falling")) d_ff_15 (
    .clk(C), .D(INPUT[14]), .Q(Q[14]), .en(WRITE), .reset(RESET));  // open: Qn, preset
  D_Flip_Flop #(.trigger("falling")) d_ff_16 (
    .clk(C), .D(INPUT[15]), .Q(Q[15]), .en(WRITE), .reset(RESET));  // open: Qn, preset
endmodule

module register_file (
  input  [3:0] rs,
  input  [15:0] DATA,
  input  [3:0] rd,
  input  [3:0] rt,
  input  WRITE,
  input  RESET,
  output [15:0] S,
  output [15:0] T
);

  wire C_out;
  wire [15:0] demultiplexer_1_out0, demultiplexer_1_out1, demultiplexer_1_out2, demultiplexer_1_out3,
       demultiplexer_1_out4, demultiplexer_1_out5, demultiplexer_1_out6, demultiplexer_1_out7,
       demultiplexer_1_out8, demultiplexer_1_out9, demultiplexer_1_out10, demultiplexer_1_out11,
       demultiplexer_1_out12, demultiplexer_1_out13, demultiplexer_1_out14, demultiplexer_1_out15,
       n16_bit_register_1_p5, n16_bit_register_2_q, n16_bit_register_3_q, n16_bit_register_4_q,
       n16_bit_register_5_q, n16_bit_register_6_q, n16_bit_register_7_q, n16_bit_register_8_q,
       n16_bit_register_9_q, n16_bit_register_10_q, n16_bit_register_11_q, n16_bit_register_12_q,
       n16_bit_register_13_q, n16_bit_register_14_q, n16_bit_register_15_q, n16_bit_register_16_q;

  Clock C (.out(C_out));
  Demultiplexer #(.select(4), .width(16), .enable("false")) demultiplexer_1 (
    .out0(demultiplexer_1_out0), .out1(demultiplexer_1_out1), .out2(demultiplexer_1_out2),
    .out3(demultiplexer_1_out3), .out4(demultiplexer_1_out4), .out5(demultiplexer_1_out5),
    .out6(demultiplexer_1_out6), .out7(demultiplexer_1_out7), .out8(demultiplexer_1_out8),
    .out9(demultiplexer_1_out9), .out10(demultiplexer_1_out10), .out11(demultiplexer_1_out11),
    .out12(demultiplexer_1_out12), .out13(demultiplexer_1_out13), .out14(demultiplexer_1_out14),
    .out15(demultiplexer_1_out15), .in(DATA), .sel(rd));
  // _16_bit_register 16_bit_register_1: pin names not known; wires that end beside it: C_out, demultiplexer_1_out0, WRITE, 1'b1, n16_bit_register_1_p5
  _16_bit_register u_16_bit_register_2 (
    .C(C_out), .INPUT(demultiplexer_1_out1), .Q(n16_bit_register_2_q), .RESET(RESET), .WRITE(WRITE));
  _16_bit_register u_16_bit_register_3 (
    .C(C_out), .INPUT(demultiplexer_1_out2), .Q(n16_bit_register_3_q), .RESET(RESET), .WRITE(WRITE));
  _16_bit_register u_16_bit_register_4 (
    .C(C_out), .INPUT(demultiplexer_1_out3), .Q(n16_bit_register_4_q), .RESET(RESET), .WRITE(WRITE));
  _16_bit_register u_16_bit_register_5 (
    .C(C_out), .INPUT(demultiplexer_1_out4), .Q(n16_bit_register_5_q), .RESET(RESET), .WRITE(WRITE));
  _16_bit_register u_16_bit_register_6 (
    .C(C_out), .INPUT(demultiplexer_1_out5), .Q(n16_bit_register_6_q), .RESET(RESET), .WRITE(WRITE));
  _16_bit_register u_16_bit_register_7 (
    .C(C_out), .INPUT(demultiplexer_1_out6), .Q(n16_bit_register_7_q), .RESET(RESET), .WRITE(WRITE));
  _16_bit_register u_16_bit_register_8 (
    .C(C_out), .INPUT(demultiplexer_1_out7), .Q(n16_bit_register_8_q), .RESET(RESET), .WRITE(WRITE));
  _16_bit_register u_16_bit_register_9 (
    .C(C_out), .INPUT(demultiplexer_1_out8), .Q(n16_bit_register_9_q), .RESET(RESET), .WRITE(WRITE));
  _16_bit_register u_16_bit_register_10 (
    .C(C_out), .INPUT(demultiplexer_1_out9), .Q(n16_bit_register_10_q), .RESET(RESET), .WRITE(WRITE));
  _16_bit_register u_16_bit_register_11 (
    .C(C_out), .INPUT(demultiplexer_1_out10), .Q(n16_bit_register_11_q), .RESET(RESET), .WRITE(WRITE));
  _16_bit_register u_16_bit_register_12 (
    .C(C_out), .INPUT(demultiplexer_1_out11), .Q(n16_bit_register_12_q), .RESET(RESET), .WRITE(WRITE));
  _16_bit_register u_16_bit_register_13 (
    .C(C_out), .INPUT(demultiplexer_1_out12), .Q(n16_bit_register_13_q), .RESET(RESET), .WRITE(WRITE));
  _16_bit_register u_16_bit_register_14 (
    .C(C_out), .INPUT(demultiplexer_1_out13), .Q(n16_bit_register_14_q), .RESET(RESET), .WRITE(WRITE));
  _16_bit_register u_16_bit_register_15 (
    .C(C_out), .INPUT(demultiplexer_1_out14), .Q(n16_bit_register_15_q), .RESET(RESET), .WRITE(WRITE));
  _16_bit_register u_16_bit_register_16 (
    .C(C_out), .INPUT(demultiplexer_1_out15), .Q(n16_bit_register_16_q), .RESET(RESET), .WRITE(WRITE));
  Multiplexer #(.select(4), .width(16), .enable("false")) multiplexer_1 (
    .in0(n16_bit_register_1_p5), .in1(n16_bit_register_2_q), .in2(n16_bit_register_3_q),
    .in3(n16_bit_register_4_q), .in4(n16_bit_register_5_q), .in5(n16_bit_register_6_q),
    .in6(n16_bit_register_7_q), .in7(n16_bit_register_8_q), .in8(n16_bit_register_9_q),
    .in9(n16_bit_register_10_q), .in10(n16_bit_register_11_q), .in11(n16_bit_register_12_q),
    .in12(n16_bit_register_13_q), .in13(n16_bit_register_14_q), .in14(n16_bit_register_15_q),
    .in15(n16_bit_register_16_q), .out(S), .sel(rs));
  Multiplexer #(.select(4), .width(16), .enable("false")) multiplexer_2 (
    .in0(n16_bit_register_1_p5), .in1(n16_bit_register_2_q), .in2(n16_bit_register_3_q),
    .in3(n16_bit_register_4_q), .in4(n16_bit_register_5_q), .in5(n16_bit_register_6_q),
    .in6(n16_bit_register_7_q), .in7(n16_bit_register_8_q), .in8(n16_bit_register_9_q),
    .in9(n16_bit_register_10_q), .in10(n16_bit_register_11_q), .in11(n16_bit_register_12_q),
    .in12(n16_bit_register_13_q), .in13(n16_bit_register_14_q), .in14(n16_bit_register_15_q), .out(T),
    .sel(rt));  // open: in15
endmodule

module counter (
  input  [15:0] D,
  input  input_D_enable,
  input  C,
  output [15:0] OUTPUT
);

  wire comparator_1_eq, comparator_1_gt, or_1_out;
  wire [15:0] controlled_buffer_1_out;

  assign controlled_buffer_1_out = input_D_enable ? D : 16'bz;  // Controlled_Buffer controlled_buffer_1
  _16_bit_register u_16_bit_register_1 (
    .C(C), .INPUT(controlled_buffer_1_out), .Q(OUTPUT), .RESET(or_1_out), .WRITE(1'b1));
  _16_bit_carry_lookahead_adder u_16_bit_carry_lookahead_adder_1 (
    .OUTPUT(controlled_buffer_1_out), .A(OUTPUT), .B(16'h1), .C(1'b0));  // open: OVERFLOW
  Comparator #(.width(16), .mode("unsigned")) comparator_1 (
    .a(OUTPUT), .b(D), .gt(comparator_1_gt), .eq(comparator_1_eq));  // open: lt
  or or_1 (or_1_out, comparator_1_gt, comparator_1_eq);

  // Notes on the sheet:
  //   RESET IF GREATER THAN OR EQUAL TO
  //   NO OVERFLOW BECAUSE OF UNSIGNED NUMERIC TYPE
endmodule

module counter_traffic_light (
  input  [15:0] D,
  input  C,
  output [15:0] OUTPUT
);

  wire comparator_1_eq, comparator_1_gt, or_1_out;
  wire [15:0] n16_bit_carry_lookahead_adder_1_output;

  _16_bit_register u_16_bit_register_1 (
    .C(C), .INPUT(n16_bit_carry_lookahead_adder_1_output), .Q(OUTPUT), .RESET(or_1_out), .WRITE(1'b1));
  _16_bit_carry_lookahead_adder u_16_bit_carry_lookahead_adder_1 (
    .OUTPUT(n16_bit_carry_lookahead_adder_1_output), .A(OUTPUT), .B(16'h1));  // open: C, OVERFLOW
  Comparator #(.width(16), .mode("unsigned")) comparator_1 (
    .a(OUTPUT), .b(D), .gt(comparator_1_gt), .eq(comparator_1_eq));  // open: lt
  or or_1 (or_1_out, comparator_1_gt, comparator_1_eq);

  // Notes on the sheet:
  //   RESET IF GREATER THAN OR EQUAL TO
  //   NO OVERFLOW BECAUSE OF UNSIGNED NUMERIC TYPE
endmodule

module finite_state_machine_traffic_light (
);

  wire CLOCK_2_out, CLOCK_out;
  wire [2:0] rom_1_data, rom_2_data;
  wire [15:0] counter_traffic_light_1_output, counter_traffic_light_2_output;

  Clock CLOCK (.out(CLOCK_out));
  Clock CLOCK_2 (.out(CLOCK_2_out));
  counter_traffic_light counter_traffic_light_1 (.D(16'h1c), .C(CLOCK_out), .OUTPUT(counter_traffic_light_1_output));
  counter_traffic_light counter_traffic_light_2 (.D(16'h1c), .C(CLOCK_2_out), .OUTPUT(counter_traffic_light_2_output));
  ROM #(.addrWidth(16), .dataWidth(3)) rom_1 (.addr(counter_traffic_light_1_output), .data(rom_1_data));  // open: sel
  ROM #(.addrWidth(16), .dataWidth(3)) rom_2 (.addr(counter_traffic_light_2_output), .data(rom_2_data));  // open: sel
  LED RED (.in(rom_1_data[0]));
  LED ORANGE (.in(rom_1_data[1]));
  LED GREEN (.in(rom_1_data[2]));
  LED RED_2 (.in(rom_2_data[0]));
  LED ORANGE_2 (.in(rom_2_data[1]));
  LED GREEN_2 (.in(rom_2_data[2]));

  // Notes on the sheet:
  //   CONSTANT RESET AFTER 28s
  //   CONSTANT RESET AFTER 28s
  //   USE TICK FREQUENCY 2Hz
  //   contents of rom_1 (hex, n*v repeats v):
  //   8*4 4*2 16*1
  //   contents of rom_2 (hex, n*v repeats v):
  //   14*1 8*4 4*2 1 1
  //   TRAFFIC LIGHT 1
  //   TRAFFIC LIGHT 2
endmodule

module fifo_stack (
  input  RESET,
  input  PUSH,
  input  POP,
  input  [15:0] DATA,
  output [15:0] TOP_OF_STACK,
  output ERROR
);

  wire CLOCK_out, comparator_1_eq, comparator_1_lt, not_1_out, or_1_out, or_2_out, or_3_out, or_4_out;
  wire [15:0] bit_extender_1_out, bit_extender_2_out, multiplexer_1_out, multiplexer_2_out,
       multiplexer_3_out, n16_bit_carry_lookahead_adder_1_output, n16_bit_register_1_q, subtractor_1_out,
       subtractor_2_out, subtractor_3_out;

  assign bit_extender_1_out = {{15{1'b0}}, POP};  // Bit_Extender bit_extender_1
  Subtractor #(.width(16)) subtractor_1 (
    .a(n16_bit_register_1_q), .b(bit_extender_1_out), .out(subtractor_1_out));  // open: bin, bout
  assign bit_extender_2_out = {{15{1'b0}}, PUSH};  // Bit_Extender bit_extender_2
  Subtractor #(.width(16)) subtractor_2 (
    .a(n16_bit_register_1_q), .b(16'h1), .out(subtractor_2_out));  // open: bin, bout
  Multiplexer #(.width(16), .enable("false")) multiplexer_1 (
    .in0(subtractor_2_out), .in1(n16_bit_register_1_q), .out(multiplexer_1_out), .sel(not_1_out));
  _16_bit_carry_lookahead_adder u_16_bit_carry_lookahead_adder_1 (
    .OUTPUT(n16_bit_carry_lookahead_adder_1_output), .A(subtractor_1_out), .B(bit_extender_2_out));  // open: C, OVERFLOW
  _16_bit_register u_16_bit_register_1 (
    .C(CLOCK_out), .INPUT(n16_bit_carry_lookahead_adder_1_output), .Q(n16_bit_register_1_q), .RESET(RESET),
    .WRITE(or_1_out));
  or or_1 (or_1_out, POP, PUSH);
  Subtractor #(.width(16)) subtractor_3 (
    .a(n16_bit_register_1_q), .b(16'h1), .out(subtractor_3_out));  // open: bin, bout
  or or_2 (or_2_out, PUSH, POP);
  not not_1 (not_1_out, POP);
  Multiplexer #(.width(16), .enable("false")) multiplexer_2 (
    .in0({16{1'b0}}), .in1(DATA), .out(multiplexer_2_out), .sel(not_1_out));
  Multiplexer #(.width(16)) multiplexer_3 (
    .in0(subtractor_3_out), .in1(multiplexer_1_out), .out(multiplexer_3_out), .sel(or_2_out));  // open: en
  or or_3 (or_3_out, PUSH, POP);
  Clock CLOCK (.out(CLOCK_out));
  RAM #(.addrWidth(16), .dataWidth(16), .bus("separate")) ram_1 (
    .addr(multiplexer_3_out), .din(multiplexer_2_out), .data(TOP_OF_STACK), .str(or_3_out), .clk(CLOCK_out),
    .ld(1'b1), .clr(RESET));  // open: sel
  Comparator #(.width(16)) comparator_1 (
    .a({16{1'b0}}), .b(n16_bit_register_1_q), .eq(comparator_1_eq), .lt(comparator_1_lt));  // open: gt
  and and_1 (ERROR, or_4_out, POP);
  or or_4 (or_4_out, comparator_1_eq, comparator_1_lt);
endmodule

module counter_2 (
  input  [15:0] \input ,
  input  input_change,
  input  reset,
  output [15:0] counter
);

  wire clock_1_out;
  wire [15:0] undriven;

  Clock clock_1 (.out(clock_1_out));
  Controlled_Buffer #(.width(16)) controlled_buffer_1 (.in(\input ), .en(input_change));  // open: out
  _16_bit_register u_16_bit_register_1 (.C(clock_1_out), .INPUT(undriven), .RESET(reset), .WRITE(1'b1));  // open: Q
endmodule
