// Logisim project resources.circ as structural Verilog: 3 circuits, main circuit immediate_unit
// IMMEDIATE UNIT
module immediate_unit (
  input  [15:0] INSTRUCTION,
  input  ORI,
  input  LUI,
  input  BRNZ,
  input  J,
  input  JR,
  input  JAL,
  output [15:0] IMMEDIATE_VALUE,
  output [2:0] out_9
);

  wire [15:0] bit_extender_1_out, bit_extender_2_out, bit_extender_3_out, bit_extender_4_out,
       bit_extender_5_out, sll_8_1_output;

  or or_1 (out_9[0], ORI, BRNZ, J, JAL);
  or or_2 (out_9[1], BRNZ, LUI);
  or or_3 (out_9[2], J, JR, JAL);
  assign bit_extender_1_out = {{8{1'b0}}, INSTRUCTION[7:0]};  // Bit_Extender bit_extender_1
  assign bit_extender_2_out = {{8{1'b0}}, INSTRUCTION[7:0]};  // Bit_Extender bit_extender_2
  sll_8 sll_8_1 (.INPUT(bit_extender_2_out), .OUTPUT(sll_8_1_output));
  assign bit_extender_3_out = {{8{INSTRUCTION[7]}}, INSTRUCTION[7:0]};  // Bit_Extender bit_extender_3
  assign bit_extender_4_out = {{12{INSTRUCTION[7]}}, INSTRUCTION[7:4]};  // Bit_Extender bit_extender_4
  assign bit_extender_5_out = {{8{INSTRUCTION[11]}}, INSTRUCTION[11:4]};  // Bit_Extender bit_extender_5
  Multiplexer #(.select(3), .width(16), .enable("false")) multiplexer_1 (
    .in0({16{1'b0}}), .in1(bit_extender_1_out), .in2(sll_8_1_output), .in3(bit_extender_3_out),
    .in4(bit_extender_4_out), .in5(bit_extender_5_out), .out(IMMEDIATE_VALUE), .sel(out_9));  // open: in6, in7
endmodule

// CONTROL UNIT
module control_unit (
  input  [15:0] INSTRUCTION,
  output [3:0] rd,
  output [3:0] rs,
  output UNKNOWN_INSTRUCTION,
  output ORI,
  output LUI,
  output BRNZ,
  output J,
  output JR,
  output JAL,
  output [3:0] rt,
  output [1:0] MemToReg,
  output MemRead,
  output MemWrite,
  output ALUSrc,
  output RegWrite,
  output ALUImm,
  output RegDst,
  output rdTOrt,
  output [3:0] ALU_OP_CODE,
  output ZERO
);

  wire ADD_out, and_2_out, and_3_out, CP_out, EQ_out, GT_out, INV_out, J_TYPE_out, LT_out, NEQ_out, NOT_out,
       or_7_out, OR_out, R_TYPE_out, SLA_out, SLL_out, SRA_out, SRL_out, SUB_out, ZERO_2_out;

  // AND_Gate ZERO has open pins: in0=INSTRUCTION[12], in1=INSTRUCTION[13], in2=INSTRUCTION[14], in3=INSTRUCTION[15], out=open
  and R_TYPE (R_TYPE_out, INSTRUCTION[12], ~INSTRUCTION[13], ~INSTRUCTION[14], ~INSTRUCTION[15]);  // AND_Gate
  // AND_Gate AND has open pins: in0=INSTRUCTION[12], in1=INSTRUCTION[13], in2=INSTRUCTION[14], in3=INSTRUCTION[15], out=open
  and OR (OR_out, INSTRUCTION[12], INSTRUCTION[13], ~INSTRUCTION[14], ~INSTRUCTION[15]);  // AND_Gate
  and ADD (ADD_out, ~INSTRUCTION[12], ~INSTRUCTION[13], INSTRUCTION[14], ~INSTRUCTION[15]);  // AND_Gate
  and SUB (SUB_out, INSTRUCTION[12], ~INSTRUCTION[13], INSTRUCTION[14], ~INSTRUCTION[15]);  // AND_Gate
  and LT (LT_out, ~INSTRUCTION[12], INSTRUCTION[13], INSTRUCTION[14], ~INSTRUCTION[15]);  // AND_Gate
  or or_2 (ALU_OP_CODE[3], EQ_out, NEQ_out, LUI, BRNZ, JAL, INV_out, CP_out, SRA_out, SLA_out, SRL_out, SLL_out);
  and GT (GT_out, INSTRUCTION[12], INSTRUCTION[13], INSTRUCTION[14], ~INSTRUCTION[15]);  // AND_Gate
  and EQ (EQ_out, ~INSTRUCTION[12], ~INSTRUCTION[13], ~INSTRUCTION[14], INSTRUCTION[15]);  // AND_Gate
  and NEQ (NEQ_out, INSTRUCTION[12], ~INSTRUCTION[13], ~INSTRUCTION[14], INSTRUCTION[15]);  // AND_Gate
  and LW (MemRead, ~INSTRUCTION[12], INSTRUCTION[13], ~INSTRUCTION[14], INSTRUCTION[15]);  // AND_Gate
  or or_3 (ALU_OP_CODE[2], ADD_out, SUB_out, LT_out, GT_out, MemRead, LUI, JAL, MemWrite, JR, CP_out, SRA_out, SLA_out, SRL_out);
  and SW (MemWrite, INSTRUCTION[12], INSTRUCTION[13], ~INSTRUCTION[14], INSTRUCTION[15]);  // AND_Gate
  and u_ORI (ORI, ~INSTRUCTION[12], ~INSTRUCTION[13], INSTRUCTION[14], INSTRUCTION[15]);  // AND_Gate
  and u_LUI (LUI, INSTRUCTION[12], ~INSTRUCTION[13], INSTRUCTION[14], INSTRUCTION[15]);  // AND_Gate
  or or_4 (ALUSrc, MemWrite, MemRead);
  and u_BRNZ (BRNZ, ~INSTRUCTION[12], INSTRUCTION[13], INSTRUCTION[14], INSTRUCTION[15]);  // AND_Gate
  and J_TYPE (J_TYPE_out, INSTRUCTION[12], INSTRUCTION[13], INSTRUCTION[14], INSTRUCTION[15]);
  or or_5 (ALU_OP_CODE[1], LT_out, GT_out, OR_out, ORI, JAL, LUI, INV_out, SLL_out, SRA_out, CP_out);
  and ZERO_2 (ZERO_2_out, ~INSTRUCTION[0], ~INSTRUCTION[1], ~INSTRUCTION[2], ~INSTRUCTION[3], R_TYPE_out);  // AND_Gate
  and NOT (NOT_out, INSTRUCTION[0], ~INSTRUCTION[1], ~INSTRUCTION[2], ~INSTRUCTION[3], R_TYPE_out);  // AND_Gate
  and INV (INV_out, ~INSTRUCTION[0], INSTRUCTION[1], ~INSTRUCTION[2], INSTRUCTION[3], R_TYPE_out);  // AND_Gate
  and SLL (SLL_out, INSTRUCTION[0], INSTRUCTION[1], ~INSTRUCTION[2], INSTRUCTION[3], R_TYPE_out);  // AND_Gate
  or or_6 (ALU_OP_CODE[0], BRNZ, LUI, NEQ_out, GT_out, SUB_out, OR_out, ORI, NOT_out, SLL_out, SLA_out, CP_out, JAL, ORI);
  and SRL (SRL_out, ~INSTRUCTION[0], ~INSTRUCTION[1], INSTRUCTION[2], INSTRUCTION[3], R_TYPE_out);  // AND_Gate
  and SLA (SLA_out, INSTRUCTION[0], ~INSTRUCTION[1], INSTRUCTION[2], INSTRUCTION[3], R_TYPE_out);  // AND_Gate
  and SRA (SRA_out, ~INSTRUCTION[0], INSTRUCTION[1], INSTRUCTION[2], INSTRUCTION[3], R_TYPE_out);  // AND_Gate
  and CP (CP_out, INSTRUCTION[0], INSTRUCTION[1], INSTRUCTION[2], INSTRUCTION[3], R_TYPE_out);
  not not_2 (RegWrite, or_7_out);
  or or_7 (or_7_out, BRNZ, J, JR, MemWrite);
  and u_J (J, ~INSTRUCTION[0], ~INSTRUCTION[1], ~INSTRUCTION[2], ~INSTRUCTION[3], J_TYPE_out);  // AND_Gate
  and u_JR (JR, ~INSTRUCTION[0], ~INSTRUCTION[1], INSTRUCTION[2], ~INSTRUCTION[3], J_TYPE_out);  // AND_Gate
  and u_JAL (JAL, INSTRUCTION[0], INSTRUCTION[1], INSTRUCTION[2], INSTRUCTION[3], J_TYPE_out);
  or or_8 (RegDst, MemWrite, ORI, BRNZ, JR);
  or or_9 (ALUImm, JR, ORI);
  and and_2 (and_2_out, R_TYPE_out, ~CP_out, ~SRA_out, ~SLA_out, ~SRL_out, ~SLL_out, ~INV_out, ~NOT_out, ~ZERO_2_out);  // AND_Gate
  and and_3 (and_3_out, J_TYPE_out, ~J, ~JR, ~JAL);  // AND_Gate
  or or_10 (MemToReg[0], MemRead, JAL);
  or or_11 (MemToReg[1], JAL, LUI);
  or or_12 (UNKNOWN_INSTRUCTION, and_2_out, and_3_out);

  assign rd = INSTRUCTION[11:8];
  assign rdTOrt = JAL;
  assign rs = INSTRUCTION[7:4];
  assign rt = INSTRUCTION[3:0];
  assign ZERO = BRNZ;
endmodule

// SLL8
module sll_8 (
  input  [15:0] INPUT,
  output [15:0] OUTPUT
);

  LED led_1 (.in(INPUT[14]));
  LED led_2 (.in(INPUT[13]));
  LED led_3 (.in(INPUT[15]));
  LED led_4 (.in(INPUT[8]));
  LED led_5 (.in(INPUT[9]));
  LED led_6 (.in(INPUT[11]));
  LED led_7 (.in(INPUT[12]));
  LED led_8 (.in(INPUT[10]));

  assign OUTPUT = {INPUT[7:0], {8{1'b0}}};
endmodule
