// Logisim project opdracht5_7_segment_display.circ as structural Verilog: 2 circuits, main circuit main
module main (
  input  [2:0] _3_BIT_INPUT
);

  wire _3_BIT_TO_7_DECODER_a, _3_BIT_TO_7_DECODER_b, _3_BIT_TO_7_DECODER_c, _3_BIT_TO_7_DECODER_d,
       _3_BIT_TO_7_DECODER_e, _3_BIT_TO_7_DECODER_f, _3_BIT_TO_7_DECODER_g;

  _7_segment_display_nand_gate _3_BIT_TO_7_DECODER (
    .a(_3_BIT_TO_7_DECODER_a), .b(_3_BIT_TO_7_DECODER_b), .c(_3_BIT_TO_7_DECODER_c),
    .d(_3_BIT_TO_7_DECODER_d), .e(_3_BIT_TO_7_DECODER_e), .f(_3_BIT_TO_7_DECODER_f),
    .g(_3_BIT_TO_7_DECODER_g), ._3_BIT_INPUT(_3_BIT_INPUT));
  _7_Segment_Display u_7_segment_display_1 (
    .g(_3_BIT_TO_7_DECODER_g), .f(_3_BIT_TO_7_DECODER_f), .a(_3_BIT_TO_7_DECODER_a),
    .b(_3_BIT_TO_7_DECODER_b), .e(_3_BIT_TO_7_DECODER_e), .d(_3_BIT_TO_7_DECODER_d), .c(_3_BIT_TO_7_DECODER_c));  // open: dp
endmodule

module _7_segment_display_nand_gate (
  input  [2:0] _3_BIT_INPUT,
  output a,
  output b,
  output c,
  output d,
  output e,
  output f,
  output g
);

  wire nand_1_out, nand_2_out, nand_3_out, nand_4_out, nand_5_out, nand_6_out, nand_7_out, nand_8_out,
       nand_9_out, nand_10_out, nand_11_out, nand_12_out, nand_13_out, nand_14_out, nand_15_out, nand_16_out,
       nand_17_out, nand_18_out, nand_19_out, nand_20_out, nand_21_out, nand_22_out, nand_23_out,
       nand_24_out, nand_25_out, nand_26_out, nand_28_out, nand_29_out, nand_30_out, nand_31_out,
       nand_32_out, nand_33_out, nand_34_out, nand_35_out, nand_36_out, nand_37_out, nand_38_out, nand_39_out;

  nand nand_1 (nand_1_out, _3_BIT_INPUT[0], _3_BIT_INPUT[0]);
  nand nand_2 (nand_2_out, _3_BIT_INPUT[2], _3_BIT_INPUT[2]);
  nand nand_3 (nand_3_out, _3_BIT_INPUT[1], _3_BIT_INPUT[1]);
  nand nand_4 (nand_4_out, _3_BIT_INPUT[2], _3_BIT_INPUT[2]);
  nand nand_5 (nand_5_out, _3_BIT_INPUT[2], _3_BIT_INPUT[2]);
  nand nand_6 (nand_6_out, _3_BIT_INPUT[0], _3_BIT_INPUT[0]);
  nand nand_7 (nand_7_out, _3_BIT_INPUT[0], _3_BIT_INPUT[0]);
  nand nand_8 (nand_8_out, _3_BIT_INPUT[2], _3_BIT_INPUT[2]);
  nand nand_9 (nand_9_out, _3_BIT_INPUT[0], _3_BIT_INPUT[0]);
  nand nand_10 (nand_10_out, _3_BIT_INPUT[2], _3_BIT_INPUT[2]);
  nand nand_11 (nand_11_out, _3_BIT_INPUT[1], _3_BIT_INPUT[1]);
  nand nand_12 (nand_12_out, _3_BIT_INPUT[0], _3_BIT_INPUT[0]);
  nand nand_13 (nand_13_out, _3_BIT_INPUT[2], _3_BIT_INPUT[2]);
  nand nand_14 (nand_14_out, _3_BIT_INPUT[2], _3_BIT_INPUT[2]);
  nand nand_15 (nand_15_out, _3_BIT_INPUT[1], _3_BIT_INPUT[1]);
  nand nand_16 (nand_16_out, _3_BIT_INPUT[2], _3_BIT_INPUT[2]);
  nand nand_17 (nand_17_out, _3_BIT_INPUT[1], _3_BIT_INPUT[1]);
  nand nand_18 (nand_18_out, _3_BIT_INPUT[2], _3_BIT_INPUT[2]);
  nand nand_19 (nand_19_out, _3_BIT_INPUT[0], _3_BIT_INPUT[0]);
  nand nand_20 (nand_20_out, _3_BIT_INPUT[1], _3_BIT_INPUT[1]);
  nand nand_21 (nand_21_out, _3_BIT_INPUT[2], _3_BIT_INPUT[2]);
  nand nand_22 (nand_22_out, nand_1_out, nand_2_out);
  nand nand_23 (nand_23_out, _3_BIT_INPUT[1], _3_BIT_INPUT[1]);
  nand nand_24 (nand_24_out, _3_BIT_INPUT[0], _3_BIT_INPUT[2]);
  nand nand_25 (nand_25_out, nand_3_out, nand_4_out);
  nand nand_26 (nand_26_out, _3_BIT_INPUT[1], _3_BIT_INPUT[2]);
  nand nand_27 (c, _3_BIT_INPUT[1], nand_5_out, nand_6_out);
  nand nand_28 (nand_28_out, nand_7_out, nand_8_out);
  nand nand_29 (nand_29_out, nand_9_out, _3_BIT_INPUT[1]);
  nand nand_30 (nand_30_out, _3_BIT_INPUT[1], nand_10_out);
  nand nand_31 (nand_31_out, _3_BIT_INPUT[0], nand_11_out, _3_BIT_INPUT[2]);
  nand nand_32 (nand_32_out, nand_12_out, nand_13_out);
  nand nand_33 (nand_33_out, _3_BIT_INPUT[1], nand_14_out);
  nand nand_34 (nand_34_out, nand_15_out, nand_16_out);
  nand nand_35 (nand_35_out, _3_BIT_INPUT[0], nand_17_out);
  nand nand_36 (nand_36_out, _3_BIT_INPUT[0], nand_18_out);
  nand nand_37 (nand_37_out, nand_19_out, _3_BIT_INPUT[1]);
  nand nand_38 (nand_38_out, _3_BIT_INPUT[0], nand_20_out);
  nand nand_39 (nand_39_out, _3_BIT_INPUT[0], nand_21_out);
  nand nand_40 (a, nand_22_out, nand_23_out, nand_24_out);
  nand nand_41 (b, _3_BIT_INPUT[0], nand_25_out, nand_26_out);
  nand nand_42 (d, nand_28_out, nand_29_out, nand_30_out, nand_31_out);
  nand nand_43 (e, nand_32_out, nand_33_out);
  nand nand_44 (f, nand_34_out, nand_35_out, nand_36_out);
  nand nand_45 (g, nand_37_out, nand_38_out, nand_39_out);
endmodule
