// Logisim project ALU.circ as structural Verilog
module main (
  output halt,
  output [8:0] counter,
  output [3:0] op,
  output [15:0] a,
  output [15:0] b,
  output [15:0] oracle,
  output [15:0] result,
  output err_oracle,
  output error,
  output ok,
  output start_delimiter
);

  wire and_1_out, and_2_out, clock_1_out, comparator_1_eq, comparator_2_eq;

  Clock clock_1 (.out(clock_1_out));
  Counter #(.width(9), .max('h1ff), .trigger("falling")) counter_1 (
    .Q(counter), .carry(halt), .clk(clock_1_out));  // open: load, D, count, clr
  RAM #(.addrWidth(12), .dataWidth(4), .bus("separate")) ram_1 (
    .addr({counter, 3'b000}), .data(op), .ld(1'b1));  // open: din, str, sel, clk, clr
  RAM #(.addrWidth(12), .dataWidth(16), .bus("separate")) ram_2 (
    .addr({counter, 3'b001}), .data(a), .ld(1'b1));  // open: din, str, sel, clk, clr
  RAM #(.addrWidth(12), .dataWidth(16), .bus("separate")) ram_3 (
    .addr({counter, 3'b010}), .data(b), .ld(1'b1));  // open: din, str, sel, clk, clr
  RAM #(.addrWidth(12), .dataWidth(16), .bus("separate")) ram_4 (
    .addr({counter, 3'b011}), .data(oracle), .ld(1'b1));  // open: din, str, sel, clk, clr
  RAM #(.addrWidth(12), .dataWidth(1), .bus("separate")) ram_5 (
    .addr({counter, 3'b100}), .data(err_oracle), .ld(1'b1));  // open: din, str, sel, clk, clr
  RAM #(.addrWidth(12), .dataWidth(1), .bus("separate")) ram_6 (
    .addr({counter, 3'b101}), .data(start_delimiter), .ld(1'b1));  // open: din, str, sel, clk, clr
  Comparator #(.width(1), .mode("unsigned")) comparator_1 (
    .a(error), .b(err_oracle), .eq(comparator_1_eq));  // open: gt, lt
  Comparator #(.width(16)) comparator_2 (.a(result), .b(oracle), .eq(comparator_2_eq));  // open: gt, lt
  and and_1 (and_1_out, comparator_1_eq, error);
  and and_2 (and_2_out, comparator_2_eq, comparator_1_eq, ~error);  // AND_Gate
  or or_1 (ok, and_1_out, and_2_out);

  // Notes on the sheet:
  //   You must complete the circuit '16-bit ALU' instead.
  //   DO NOT EDIT THIS CIRCUIT!
endmodule

module _16_bit_ALU (
  input  [3:0] ALU_code,
  input  [15:0] a,
  input  [15:0] b,
  output [15:0] result,
  output overflow
);

  wire adder_1_cout, bit_extender_5_out, comparator_1_lt, comparator_2_eq, comparator_3_eq, comparator_4_gt,
       not_2_out, sub_1_out_4;
  wire [15:0] adder_1_out, and_out, bit_extender_1_out, bit_extender_2_out, bit_extender_3_out,
       bit_extender_4_out, multiplier_1_cout, multiplier_1_out, negator_1_out, not_out, or_out,
       shifter_1_out, shifter_2_out, shifter_3_out, sub_1_out_3;

  assign not_out = ~a;  // NOT_Gate not, 16 bits wide
  assign and_out = a & b;  // AND_Gate and, 16 bits wide
  assign or_out = a | b;  // OR_Gate or, 16 bits wide
  Adder #(.width(16)) adder_1 (.a(a), .b(b), .out(adder_1_out), .cout(adder_1_cout));  // open: cin
  sub sub_1 (.\input (a), .input_2(b), .out_3(sub_1_out_3), .out_4(sub_1_out_4));
  Comparator #(.width(16)) comparator_1 (.a(a), .b(b), .lt(comparator_1_lt));  // open: gt, eq
  Comparator #(.width(16)) comparator_2 (.a(a), .b(b), .eq(comparator_2_eq));  // open: gt, lt
  Comparator #(.width(16)) comparator_3 (.a(a), .b(b), .eq(comparator_3_eq));  // open: gt, lt
  Negator #(.width(16)) negator_1 (.in(a), .out(negator_1_out));
  Shifter #(.width(16)) shifter_1 (.in(a), .\dist (4'b0001), .out(shifter_1_out));
  Shifter #(.width(16), .shift("lr")) shifter_2 (.in(a), .\dist (4'b0001), .out(shifter_2_out));
  Multiplier #(.width(16)) multiplier_1 (
    .a(a), .b(16'h2), .out(multiplier_1_out), .cout(multiplier_1_cout));  // open: cin
  Shifter #(.width(16), .shift("ar")) shifter_3 (.in(a), .\dist (4'b0001), .out(shifter_3_out));
  assign bit_extender_1_out = {{15{1'b0}}, comparator_1_lt};  // Bit_Extender bit_extender_1
  Comparator #(.width(16)) comparator_4 (.a(a), .b(b), .gt(comparator_4_gt));  // open: eq, lt
  not not_2 (not_2_out, comparator_3_eq);
  assign bit_extender_2_out = {{15{1'b0}}, comparator_4_gt};  // Bit_Extender bit_extender_2
  assign bit_extender_3_out = {{15{1'b0}}, comparator_2_eq};  // Bit_Extender bit_extender_3
  assign bit_extender_4_out = {{15{1'b0}}, not_2_out};  // Bit_Extender bit_extender_4
  Bit_Extender #(.in_width(16), .out_width(1)) bit_extender_5 (.in(multiplier_1_cout), .out(bit_extender_5_out));
  Multiplexer #(.select(4), .width(16), .enable("false")) multiplexer_1 (
    .in0({16{1'b0}}), .in1(not_out), .in2(and_out), .in3(or_out), .in4(adder_1_out), .in5(sub_1_out_3),
    .in6(bit_extender_1_out), .in7(bit_extender_2_out), .in8(bit_extender_3_out), .in9(bit_extender_4_out),
    .in10(negator_1_out), .in11(shifter_1_out), .in12(shifter_2_out), .in13(multiplier_1_out),
    .in14(shifter_3_out), .in15(a), .out(result), .sel(ALU_code));
  Multiplexer #(.select(4), .enable("false")) multiplexer_2 (
    .in0(1'b0), .in1(1'b0), .in2(1'b0), .in3(1'b0), .in4(adder_1_cout), .in5(sub_1_out_4), .in6(1'b0),
    .in7(1'b0), .in8(1'b0), .in9(1'b0), .in10(1'b0), .in11(1'b0), .in12(1'b0), .in13(bit_extender_5_out),
    .in14(1'b0), .in15(1'b0), .out(overflow), .sel(ALU_code));

  // Other names for the same wires on the sheet: MUX[3:0] = ALU_code

  // Notes on the sheet:
  //   This circuit is used as a block in the main circuit, and its layout must remain unchanged. The circuit called "main" should be the main circuit of this file.
  //   Do not change the circuit appearance.
  //   Invert 1 foutmeldign
  //   Shift left Arithemtic
  //   DO NOT CHANGE THE INPUTS AND OUTPUTS OF THIS CIRCUIT!
  //   Do not add/remove inputs or outputs. Do not even change their location or orientation.
endmodule

module lt (
  input  [15:0] input_A,
  input  [15:0] input_B,
  output [15:0] \output 
);

  wire and_1_out, and_2_out, and_3_out, and_4_out, and_5_out, and_6_out, and_7_out, and_8_out, and_9_out,
       and_10_out, and_11_out, and_12_out, and_13_out, and_14_out, and_15_out, and_16_out, not_1_out,
       not_2_out, not_3_out, not_4_out, not_5_out, not_6_out, not_7_out, not_8_out, not_9_out, not_10_out,
       not_11_out, not_12_out, not_13_out, not_14_out, not_15_out, not_16_out, not_17_out, or_1_out;

  not not_1 (not_1_out, input_B[0]);
  not not_2 (not_2_out, input_B[1]);
  not not_3 (not_3_out, input_B[2]);
  not not_4 (not_4_out, input_B[3]);
  not not_5 (not_5_out, input_B[4]);
  not not_6 (not_6_out, input_B[5]);
  not not_7 (not_7_out, input_B[6]);
  not not_8 (not_8_out, input_B[7]);
  not not_9 (not_9_out, input_B[8]);
  not not_10 (not_10_out, input_B[9]);
  not not_11 (not_11_out, input_B[10]);
  not not_12 (not_12_out, input_B[11]);
  not not_13 (not_13_out, input_B[12]);
  not not_14 (not_14_out, input_B[13]);
  not not_15 (not_15_out, input_B[14]);
  not not_16 (not_16_out, input_B[15]);
  and and_1 (and_1_out, input_A[0], not_1_out);
  and and_2 (and_2_out, input_A[1], not_2_out);
  and and_3 (and_3_out, input_A[2], not_3_out);
  and and_4 (and_4_out, input_A[3], not_4_out);
  and and_5 (and_5_out, input_A[4], not_5_out);
  and and_6 (and_6_out, input_A[5], not_6_out);
  and and_7 (and_7_out, input_A[6], not_7_out);
  and and_8 (and_8_out, input_A[7], not_8_out);
  and and_9 (and_9_out, input_A[8], not_9_out);
  and and_10 (and_10_out, input_A[9], not_10_out);
  and and_11 (and_11_out, input_A[10], not_11_out);
  and and_12 (and_12_out, input_A[11], not_12_out);
  and and_13 (and_13_out, input_A[12], not_13_out);
  and and_14 (and_14_out, input_A[13], not_14_out);
  and and_15 (and_15_out, input_A[14], not_15_out);
  and and_16 (and_16_out, input_A[15], not_16_out);
  or or_1 (or_1_out, and_1_out, and_2_out, and_3_out, and_4_out, and_5_out, and_6_out, and_7_out, and_8_out, and_9_out, and_10_out, and_11_out, and_12_out, and_13_out, and_14_out, and_15_out, and_16_out);
  assign \output  = {{15{1'b0}}, not_17_out};  // Bit_Extender bit_extender_1
  not not_17 (not_17_out, or_1_out);

  // Notes on the sheet:
  //   TRUE = 1
  //   FALSE := 0
endmodule

module gt (
  input  [15:0] input_A,
  input  [15:0] input_B,
  output [15:0] \output 
);

  wire and_1_out, and_2_out, and_3_out, and_4_out, and_5_out, and_6_out, and_7_out, and_8_out, and_9_out,
       and_10_out, and_11_out, and_12_out, and_13_out, and_14_out, and_15_out, and_16_out, not_1_out,
       not_2_out, not_3_out, not_4_out, not_5_out, not_6_out, not_7_out, not_8_out, not_9_out, not_10_out,
       not_11_out, not_12_out, not_13_out, not_14_out, not_15_out, not_16_out, or_1_out;

  not not_1 (not_1_out, input_B[0]);
  not not_2 (not_2_out, input_B[1]);
  not not_3 (not_3_out, input_B[2]);
  not not_4 (not_4_out, input_B[3]);
  not not_5 (not_5_out, input_B[4]);
  not not_6 (not_6_out, input_B[5]);
  not not_7 (not_7_out, input_B[6]);
  not not_8 (not_8_out, input_B[7]);
  not not_9 (not_9_out, input_B[8]);
  not not_10 (not_10_out, input_B[9]);
  not not_11 (not_11_out, input_B[10]);
  not not_12 (not_12_out, input_B[11]);
  not not_13 (not_13_out, input_B[12]);
  not not_14 (not_14_out, input_B[13]);
  not not_15 (not_15_out, input_B[14]);
  not not_16 (not_16_out, input_B[15]);
  and and_1 (and_1_out, input_A[0], not_1_out);
  and and_2 (and_2_out, input_A[1], not_2_out);
  and and_3 (and_3_out, input_A[2], not_3_out);
  and and_4 (and_4_out, input_A[3], not_4_out);
  and and_5 (and_5_out, input_A[4], not_5_out);
  and and_6 (and_6_out, input_A[5], not_6_out);
  and and_7 (and_7_out, input_A[6], not_7_out);
  and and_8 (and_8_out, input_A[7], not_8_out);
  and and_9 (and_9_out, input_A[8], not_9_out);
  and and_10 (and_10_out, input_A[9], not_10_out);
  and and_11 (and_11_out, input_A[10], not_11_out);
  and and_12 (and_12_out, input_A[11], not_12_out);
  and and_13 (and_13_out, input_A[12], not_13_out);
  and and_14 (and_14_out, input_A[13], not_14_out);
  and and_15 (and_15_out, input_A[14], not_15_out);
  and and_16 (and_16_out, input_A[15], not_16_out);
  or or_1 (or_1_out, and_1_out, and_2_out, and_3_out, and_4_out, and_5_out, and_6_out, and_7_out, and_8_out, and_9_out, and_10_out, and_11_out, and_12_out, and_13_out, and_14_out, and_15_out, and_16_out);
  assign \output  = {{15{1'b0}}, or_1_out};  // Bit_Extender bit_extender_1

  // Notes on the sheet:
  //   TRUE = 1
  //   FALSE := 0
endmodule

module eq (
  input  [15:0] input_A,
  input  [15:0] input_B,
  output [15:0] \output 
);

  wire not_1_out, or_1_out, xor_1_out, xor_2_out, xor_3_out, xor_4_out, xor_5_out, xor_6_out, xor_7_out,
       xor_8_out, xor_9_out, xor_10_out, xor_11_out, xor_12_out, xor_13_out, xor_14_out, xor_15_out,
       xor_16_out;

  xor xor_1 (xor_1_out, input_A[0], input_B[0]);
  xor xor_2 (xor_2_out, input_A[1], input_B[1]);
  xor xor_3 (xor_3_out, input_A[2], input_B[2]);
  xor xor_4 (xor_4_out, input_A[3], input_B[3]);
  xor xor_5 (xor_5_out, input_A[4], input_B[4]);
  xor xor_6 (xor_6_out, input_A[5], input_B[5]);
  xor xor_7 (xor_7_out, input_A[6], input_B[6]);
  xor xor_8 (xor_8_out, input_A[7], input_B[7]);
  xor xor_9 (xor_9_out, input_A[8], input_B[8]);
  xor xor_10 (xor_10_out, input_A[9], input_B[9]);
  xor xor_11 (xor_11_out, input_A[10], input_B[10]);
  xor xor_12 (xor_12_out, input_A[11], input_B[11]);
  xor xor_13 (xor_13_out, input_A[12], input_B[12]);
  xor xor_14 (xor_14_out, input_A[13], input_B[13]);
  xor xor_15 (xor_15_out, input_A[14], input_B[14]);
  xor xor_16 (xor_16_out, input_A[15], input_B[15]);
  or or_1 (or_1_out, xor_1_out, xor_2_out, xor_3_out, xor_4_out, xor_5_out, xor_6_out, xor_7_out, xor_8_out, xor_9_out, xor_10_out, xor_11_out, xor_12_out, xor_13_out, xor_14_out, xor_15_out, xor_16_out);
  not not_1 (not_1_out, or_1_out);
  assign \output  = {{15{1'b0}}, not_1_out};  // Bit_Extender bit_extender_1

  // Notes on the sheet:
  //   TRUE = 1
  //   FALSE := 0
endmodule

module neq (
  input  [15:0] input_A,
  input  [15:0] input_B,
  output [15:0] \output 
);

  wire or_1_out, xor_1_out, xor_2_out, xor_3_out, xor_4_out, xor_5_out, xor_6_out, xor_7_out, xor_8_out,
       xor_9_out, xor_10_out, xor_11_out, xor_12_out, xor_13_out, xor_14_out, xor_15_out, xor_16_out;

  xor xor_1 (xor_1_out, input_A[0], input_B[0]);
  xor xor_2 (xor_2_out, input_A[1], input_B[1]);
  xor xor_3 (xor_3_out, input_A[2], input_B[2]);
  xor xor_4 (xor_4_out, input_A[3], input_B[3]);
  xor xor_5 (xor_5_out, input_A[4], input_B[4]);
  xor xor_6 (xor_6_out, input_A[5], input_B[5]);
  xor xor_7 (xor_7_out, input_A[6], input_B[6]);
  xor xor_8 (xor_8_out, input_A[7], input_B[7]);
  xor xor_9 (xor_9_out, input_A[8], input_B[8]);
  xor xor_10 (xor_10_out, input_A[9], input_B[9]);
  xor xor_11 (xor_11_out, input_A[10], input_B[10]);
  xor xor_12 (xor_12_out, input_A[11], input_B[11]);
  xor xor_13 (xor_13_out, input_A[12], input_B[12]);
  xor xor_14 (xor_14_out, input_A[13], input_B[13]);
  xor xor_15 (xor_15_out, input_A[14], input_B[14]);
  xor xor_16 (xor_16_out, input_A[15], input_B[15]);
  or or_1 (or_1_out, xor_1_out, xor_2_out, xor_3_out, xor_4_out, xor_5_out, xor_6_out, xor_7_out, xor_8_out, xor_9_out, xor_10_out, xor_11_out, xor_12_out, xor_13_out, xor_14_out, xor_15_out, xor_16_out);
  assign \output  = {{15{1'b0}}, or_1_out};  // Bit_Extender bit_extender_1

  // Notes on the sheet:
  //   TRUE = 1
  //   FALSE := 0
endmodule

module sll (
  input  [15:0] input_A,
  output [15:0] \output 
);

  wire and_1_out, and_3_out, and_4_out, and_5_out, and_6_out, and_7_out, and_8_out, and_9_out, and_10_out,
       and_11_out, and_12_out, and_13_out, and_14_out, and_15_out, and_16_out, and_17_out, and_18_out,
       and_19_out, and_20_out, and_21_out, and_22_out, and_23_out, and_24_out, and_25_out, and_26_out,
       and_27_out, and_28_out, and_30_out, not_1_out;

  not not_1 (not_1_out, 1'b1);
  and and_1 (and_1_out, input_A[0], 1'b1);
  and and_2 (\output [0], not_1_out, input_A[1]);
  and and_3 (and_3_out, input_A[1], 1'b1);
  and and_4 (and_4_out, not_1_out, input_A[2]);
  and and_5 (and_5_out, input_A[2], 1'b1);
  and and_6 (and_6_out, not_1_out, input_A[3]);
  and and_7 (and_7_out, input_A[3], 1'b1);
  and and_8 (and_8_out, not_1_out, input_A[4]);
  and and_9 (and_9_out, input_A[4], 1'b1);
  and and_10 (and_10_out, not_1_out, input_A[5]);
  and and_11 (and_11_out, input_A[5], 1'b1);
  and and_12 (and_12_out, not_1_out, input_A[6]);
  and and_13 (and_13_out, input_A[6], 1'b1);
  and and_14 (and_14_out, not_1_out, input_A[7]);
  and and_15 (and_15_out, input_A[7], 1'b1);
  and and_16 (and_16_out, not_1_out, input_A[8]);
  and and_17 (and_17_out, input_A[8], 1'b1);
  and and_18 (and_18_out, not_1_out, input_A[9]);
  and and_19 (and_19_out, input_A[9], 1'b1);
  and and_20 (and_20_out, not_1_out, input_A[10]);
  and and_21 (and_21_out, input_A[10], 1'b1);
  and and_22 (and_22_out, not_1_out, input_A[11]);
  and and_23 (and_23_out, input_A[11], 1'b1);
  and and_24 (and_24_out, not_1_out, input_A[12]);
  and and_25 (and_25_out, input_A[12], 1'b1);
  and and_26 (and_26_out, not_1_out, input_A[13]);
  and and_27 (and_27_out, input_A[13], 1'b1);
  and and_28 (and_28_out, not_1_out, input_A[14]);
  and and_29 (\output [15], input_A[14], 1'b1);
  and and_30 (and_30_out, input_A[15], not_1_out);
  or or_1 (\output [1], and_1_out, and_4_out);
  or or_2 (\output [2], and_3_out, and_6_out);
  or or_3 (\output [3], and_5_out, and_8_out);
  or or_4 (\output [4], and_7_out, and_10_out);
  or or_5 (\output [5], and_9_out, and_12_out);
  or or_6 (\output [6], and_11_out, and_14_out);
  or or_7 (\output [7], and_13_out, and_16_out);
  or or_8 (\output [8], and_15_out, and_18_out);
  or or_9 (\output [9], and_17_out, and_20_out);
  or or_10 (\output [10], and_19_out, and_22_out);
  or or_11 (\output [11], and_21_out, and_24_out);
  or or_12 (\output [12], and_23_out, and_26_out);
  or or_13 (\output [13], and_25_out, and_28_out);
  or or_14 (\output [14], and_27_out, and_30_out);
endmodule

module srl (
  input  [15:0] input_A,
  output [15:0] \output 
);

  wire and_1_out, and_3_out, and_4_out, and_5_out, and_6_out, and_7_out, and_8_out, and_9_out, and_10_out,
       and_11_out, and_12_out, and_13_out, and_14_out, and_15_out, and_16_out, and_17_out, and_18_out,
       and_19_out, and_20_out, and_21_out, and_22_out, and_23_out, and_24_out, and_25_out, and_26_out,
       and_27_out, and_28_out, and_30_out, not_1_out;

  not not_1 (not_1_out, 1'b0);
  and and_1 (and_1_out, input_A[0], 1'b0);
  and and_2 (\output [0], not_1_out, input_A[1]);
  and and_3 (and_3_out, input_A[1], 1'b0);
  and and_4 (and_4_out, not_1_out, input_A[2]);
  and and_5 (and_5_out, input_A[2], 1'b0);
  and and_6 (and_6_out, not_1_out, input_A[3]);
  and and_7 (and_7_out, input_A[3], 1'b0);
  and and_8 (and_8_out, not_1_out, input_A[4]);
  and and_9 (and_9_out, input_A[4], 1'b0);
  and and_10 (and_10_out, not_1_out, input_A[5]);
  and and_11 (and_11_out, input_A[5], 1'b0);
  and and_12 (and_12_out, not_1_out, input_A[6]);
  and and_13 (and_13_out, input_A[6], 1'b0);
  and and_14 (and_14_out, not_1_out, input_A[7]);
  and and_15 (and_15_out, input_A[7], 1'b0);
  and and_16 (and_16_out, not_1_out, input_A[8]);
  and and_17 (and_17_out, input_A[8], 1'b0);
  and and_18 (and_18_out, not_1_out, input_A[9]);
  and and_19 (and_19_out, input_A[9], 1'b0);
  and and_20 (and_20_out, not_1_out, input_A[10]);
  and and_21 (and_21_out, input_A[10], 1'b0);
  and and_22 (and_22_out, not_1_out, input_A[11]);
  and and_23 (and_23_out, input_A[11], 1'b0);
  and and_24 (and_24_out, not_1_out, input_A[12]);
  and and_25 (and_25_out, input_A[12], 1'b0);
  and and_26 (and_26_out, not_1_out, input_A[13]);
  and and_27 (and_27_out, input_A[13], 1'b0);
  and and_28 (and_28_out, not_1_out, input_A[14]);
  and and_29 (\output [15], input_A[14], 1'b0);
  and and_30 (and_30_out, input_A[15], not_1_out);
  or or_1 (\output [1], and_1_out, and_4_out);
  or or_2 (\output [2], and_3_out, and_6_out);
  or or_3 (\output [3], and_5_out, and_8_out);
  or or_4 (\output [4], and_7_out, and_10_out);
  or or_5 (\output [5], and_9_out, and_12_out);
  or or_6 (\output [6], and_11_out, and_14_out);
  or or_7 (\output [7], and_13_out, and_16_out);
  or or_8 (\output [8], and_15_out, and_18_out);
  or or_9 (\output [9], and_17_out, and_20_out);
  or or_10 (\output [10], and_19_out, and_22_out);
  or or_11 (\output [11], and_21_out, and_24_out);
  or or_12 (\output [12], and_23_out, and_26_out);
  or or_13 (\output [13], and_25_out, and_28_out);
  or or_14 (\output [14], and_27_out, and_30_out);
endmodule

module sla (
  input  [15:0] input_A,
  output [15:0] out_2,
  output overflow
);


  assign out_2 = {input_A[14:0], input_A[15]};
  assign overflow = input_A[15];
endmodule

module sra (
  input  [15:0] input_A,
  output [15:0] out_2
);

  LED led_1 (.in(input_A[0]));

  assign out_2 = {1'b0, input_A[15:1]};
endmodule

module sub (
  input  [15:0] \input ,
  input  [15:0] input_2,
  output [15:0] out_3,
  output out_4
);

  wire [15:0] negator_1_out;

  Negator #(.width(16)) negator_1 (.in(input_2), .out(negator_1_out));
  _16_bit_carry_lookahead_adder u_16_bit_carry_lookahead_adder_1 (
    .out_3(out_3), .overflow(out_4), .in_1(\input ), .in_2(negator_1_out));
endmodule
